# Fritzing sketch supla_595_16x16 (saved by Fritzing 0.9.3b)
circuit board: 8.46667cm x 5.64444cm
breadboards: 1

parts:
  WeMos_D1_Mini1 = WeMos D1 Mini
  U1 = 74HC595 [part_number=1-8 package="DIP16 [THT]"]
  LED1 = smd LED [color="Red (633nm)" package="1206 [SMD]"]
  LED2 = smd LED [color="Red (633nm)" package="1206 [SMD]"]
  LED3 = smd LED [color="Red (633nm)" package="1206 [SMD]"]
  LED4 = smd LED [color="Red (633nm)" package="1206 [SMD]"]
  LED5 = smd LED [color="Red (633nm)" package="1206 [SMD]"]
  LED6 = smd LED [color="Red (633nm)" package="1206 [SMD]"]
  LED7 = smd LED [color="Red (633nm)" package="1206 [SMD]"]
  LED8 = smd LED [color="Red (633nm)" package="1206 [SMD]"]
  R9 = Resistor [tolerance=±5% resistance=220 package=THT]
  R2 = Resistor [tolerance=±5% resistance=220 package=THT]
  R3 = Resistor [tolerance=±5% resistance=220 package=THT]
  R4 = Resistor [tolerance=±5% resistance=220 package=THT]
  R5 = Resistor [tolerance=±5% resistance=220 package=THT]
  R6 = Resistor [tolerance=±5% resistance=220 package=THT]
  R7 = Resistor [tolerance=±5% resistance=220 package=THT]
  R8 = Resistor [tolerance=±5% resistance=220 package=THT]
  U2 = 74HC595 [part_number=9-16 package="DIP16 [THT]"]
  LED9 = smd LED [color="Red (633nm)" package="1206 [SMD]"]
  LED10 = smd LED [color="Red (633nm)" package="1206 [SMD]"]
  LED11 = smd LED [color="Red (633nm)" package="1206 [SMD]"]
  LED12 = smd LED [color="Red (633nm)" package="1206 [SMD]"]
  LED13 = smd LED [color="Red (633nm)" package="1206 [SMD]"]
  LED14 = smd LED [color="Red (633nm)" package="1206 [SMD]"]
  LED15 = smd LED [color="Red (633nm)" package="1206 [SMD]"]
  LED16 = smd LED [color="Red (633nm)" package="1206 [SMD]"]
  R12 = Resistor [tolerance=±5% resistance=220 package=THT]
  R13 = Resistor [tolerance=±5% resistance=220 package=THT]
  R14 = Resistor [tolerance=±5% resistance=220 package=THT]
  R15 = Resistor [tolerance=±5% resistance=220 package=THT]
  R16 = Resistor [tolerance=±5% resistance=220 package=THT]
  R17 = Resistor [tolerance=±5% resistance=220 package=THT]
  R18 = Resistor [tolerance=±5% resistance=220 package=THT]
  R19 = Resistor [tolerance=±5% resistance=220 package=THT]
  R20 = Resistor [tolerance=±5% resistance=1k package=THT]
  R21 = Resistor [tolerance=±5% resistance=1k package=THT]
  R22 = Resistor [tolerance=±5% resistance=1k package=THT]
  R23 = Resistor [tolerance=±5% resistance=1k package=THT]
  R24 = Resistor [tolerance=±5% resistance=1k package=THT]
  R25 = Resistor [tolerance=±5% resistance=1k package=THT]
  R26 = Resistor [tolerance=±5% resistance=1k package=THT]
  R27 = Resistor [tolerance=±5% resistance=1k package=THT]
  S16 = Pushbutton [package="[THT]"]
  S15 = Pushbutton [package="[THT]"]
  S14 = Pushbutton [package="[THT]"]
  S13 = Pushbutton [package="[THT]"]
  S12 = Pushbutton [package="[THT]"]
  S11 = Pushbutton [package="[THT]"]
  S10 = Pushbutton [package="[THT]"]
  S9 = Pushbutton [package="[THT]"]
  S7 = Pushbutton [package="[THT]"]
  S6 = Pushbutton [package="[THT]"]
  S5 = Pushbutton [package="[THT]"]
  S4 = Pushbutton [package="[THT]"]
  S3 = Pushbutton [package="[THT]"]
  S2 = Pushbutton [package="[THT]"]
  S1 = Pushbutton [package="[THT]"]
  S8 = Pushbutton [package="[THT]"]

nets:
  3V3: WeMos_D1_Mini1.3V3, U1.MR, U1.VCC
  5V: WeMos_D1_Mini1.5V
  N1: WeMos_D1_Mini1.A0, S14.Pin_3, S14.Pin_4
  N2: WeMos_D1_Mini1.D0, U1.SH_CP, U2.SH_CP
  N3: WeMos_D1_Mini1.D1, S1.Pin_4
  N4: WeMos_D1_Mini1.D2, S2.Pin_4
  N5: WeMos_D1_Mini1.D3, U1.ST_CP, U2.ST_CP
  N6: WeMos_D1_Mini1.D4, S3.Pin_4
  N7: WeMos_D1_Mini1.D5, S4.Pin_3, S4.Pin_4
  N8: WeMos_D1_Mini1.D6, S5.Pin_3, S5.Pin_4
  N9: WeMos_D1_Mini1.D7, S6.Pin_3, S6.Pin_4
  N10: WeMos_D1_Mini1.D8, U1.DS
  GND: WeMos_D1_Mini1.G, U1.GND, U1.OE, R9.Pin_0, R2.Pin_0, R3.Pin_0, R4.Pin_0, R5.Pin_0, R6.Pin_0, R7.Pin_0, R8.Pin_0, R27.Pin_1
  N11: WeMos_D1_Mini1.RX, S7.Pin_4
  N12: WeMos_D1_Mini1.TX, S8.Pin_4
  N13: U1.Q1, LED1.anode
  N14: U1.Q2, LED2.anode
  N15: U1.Q3, LED3.anode
  N16: U1.Q4, LED4.anode
  N17: U1.Q5, LED5.anode
  N18: U1.Q6, LED6.anode
  N19: U1.Q7, LED7.anode
  N20: U1.Q7', U2.DS
  N21: U1.Q0, LED8.anode
  N22: LED1.cathode, R2.Pin_1
  N23: LED2.cathode, R3.Pin_1
  N24: LED3.cathode, R4.Pin_1
  N25: LED4.cathode, R5.Pin_1
  N26: LED5.cathode, R6.Pin_1
  N27: LED6.cathode, R7.Pin_1
  N28: LED7.cathode, R8.Pin_1
  N29: LED8.cathode, R9.Pin_1
  N30: U2.Q1, LED16.anode
  N31: U2.Q2, LED15.anode
  N32: U2.Q3, LED14.anode
  N33: U2.Q4, LED13.anode
  N34: U2.Q5, LED12.anode
  N35: U2.Q6, LED11.anode
  N36: U2.Q7, LED10.anode
  N37: U2.GND, U2.OE, R12.Pin_0, R13.Pin_0, R14.Pin_0, R15.Pin_0, R16.Pin_0, R17.Pin_0, R18.Pin_0, R19.Pin_0
  N38: U2.MR, U2.VCC, R20.Pin_0, S16.Pin_1, S16.Pin_2
  N39: U2.Q0, LED9.anode
  N40: LED9.cathode, R19.Pin_1
  N41: LED10.cathode, R12.Pin_1
  N42: LED11.cathode, R13.Pin_1
  N43: LED12.cathode, R14.Pin_1
  N44: LED13.cathode, R15.Pin_1
  N45: LED14.cathode, R16.Pin_1
  N46: LED15.cathode, R17.Pin_1
  N47: LED16.cathode, R18.Pin_1
  N48: R21.Pin_0, S15.Pin_1, S15.Pin_2
  N49: R22.Pin_0, S14.Pin_1, S14.Pin_2
  N50: R23.Pin_0, S13.Pin_1, S13.Pin_2
  N51: R24.Pin_0, S12.Pin_1, S12.Pin_2
  N52: R25.Pin_0, S11.Pin_1, S11.Pin_2
  N53: R26.Pin_0, S10.Pin_1, S10.Pin_2
  N54: R27.Pin_0, S9.Pin_1, S9.Pin_2
