# Fritzing sketch supla_595_8x16 (saved by Fritzing 0.9.3b)
circuit board: 8.46667cm x 5.64444cm
breadboards: 1

parts:
  WeMos_D1_Mini1 = WeMos D1 Mini
  U1 = 74HC595 [part_number=1-8 package="DIP16 [THT]"]
  LED1 = smd LED [color="Red (633nm)" package="1206 [SMD]"]
  LED2 = smd LED [color="Red (633nm)" package="1206 [SMD]"]
  LED3 = smd LED [color="Red (633nm)" package="1206 [SMD]"]
  LED4 = smd LED [color="Red (633nm)" package="1206 [SMD]"]
  LED5 = smd LED [color="Red (633nm)" package="1206 [SMD]"]
  LED6 = smd LED [color="Red (633nm)" package="1206 [SMD]"]
  LED7 = smd LED [color="Red (633nm)" package="1206 [SMD]"]
  LED8 = smd LED [color="Red (633nm)" package="1206 [SMD]"]
  R9 = Resistor [tolerance=±5% resistance=220 package=THT]
  R2 = Resistor [tolerance=±5% resistance=220 package=THT]
  R3 = Resistor [tolerance=±5% resistance=220 package=THT]
  R4 = Resistor [tolerance=±5% resistance=220 package=THT]
  R5 = Resistor [tolerance=±5% resistance=220 package=THT]
  R6 = Resistor [tolerance=±5% resistance=220 package=THT]
  R7 = Resistor [tolerance=±5% resistance=220 package=THT]
  R8 = Resistor [tolerance=±5% resistance=220 package=THT]
  R10 = Temperature Sensor (Thermistor) [thermistor_type=NTC package=THT]
  R11 = Resistor [tolerance=±5% resistance=100k package="0603 [SMD]"]
  U2 = 74HC595 [part_number=9-16 package="DIP16 [THT]"]
  LED9 = smd LED [color="Red (633nm)" package="1206 [SMD]"]
  LED10 = smd LED [color="Red (633nm)" package="1206 [SMD]"]
  LED11 = smd LED [color="Red (633nm)" package="1206 [SMD]"]
  LED12 = smd LED [color="Red (633nm)" package="1206 [SMD]"]
  LED13 = smd LED [color="Red (633nm)" package="1206 [SMD]"]
  LED14 = smd LED [color="Red (633nm)" package="1206 [SMD]"]
  LED15 = smd LED [color="Red (633nm)" package="1206 [SMD]"]
  LED16 = smd LED [color="Red (633nm)" package="1206 [SMD]"]
  R12 = Resistor [tolerance=±5% resistance=220 package=THT]
  R13 = Resistor [tolerance=±5% resistance=220 package=THT]
  R14 = Resistor [tolerance=±5% resistance=220 package=THT]
  R15 = Resistor [tolerance=±5% resistance=220 package=THT]
  R16 = Resistor [tolerance=±5% resistance=220 package=THT]
  R17 = Resistor [tolerance=±5% resistance=220 package=THT]
  R18 = Resistor [tolerance=±5% resistance=220 package=THT]
  R19 = Resistor [tolerance=±5% resistance=220 package=THT]

nets:
  VCC: WeMos_D1_Mini1.3V3, U1.MR, U1.VCC, R11.Pin_0, U2.MR, U2.VCC
  N1: WeMos_D1_Mini1.A0, R10.pin_0, R11.Pin_1
  N2: WeMos_D1_Mini1.D0, U1.SH_CP, U2.SH_CP
  N3: WeMos_D1_Mini1.D3, U1.ST_CP, U2.ST_CP
  N4: WeMos_D1_Mini1.D8, U1.DS
  N5: WeMos_D1_Mini1.G, U1.GND, U1.OE, R9.Pin_0, R2.Pin_0, R3.Pin_0, R4.Pin_0, R5.Pin_0, R6.Pin_0, R7.Pin_0, R8.Pin_0, R10.pin_1
  N6: U1.Q1, LED1.anode
  N7: U1.Q2, LED2.anode
  N8: U1.Q3, LED3.anode
  N9: U1.Q4, LED4.anode
  N10: U1.Q5, LED5.anode
  N11: U1.Q6, LED6.anode
  N12: U1.Q7, LED7.anode
  N13: U1.Q7', U2.DS
  N14: U1.Q0, LED8.anode
  N15: LED1.cathode, R2.Pin_1
  N16: LED2.cathode, R3.Pin_1
  N17: LED3.cathode, R4.Pin_1
  N18: LED4.cathode, R5.Pin_1
  N19: LED5.cathode, R6.Pin_1
  N20: LED6.cathode, R7.Pin_1
  N21: LED7.cathode, R8.Pin_1
  N22: LED8.cathode, R9.Pin_1
  N23: U2.Q1, LED16.anode
  N24: U2.Q2, LED15.anode
  N25: U2.Q3, LED14.anode
  N26: U2.Q4, LED13.anode
  N27: U2.Q5, LED12.anode
  N28: U2.Q6, LED11.anode
  N29: U2.Q7, LED10.anode
  N30: U2.GND, U2.OE, R12.Pin_0, R13.Pin_0, R14.Pin_0, R15.Pin_0, R16.Pin_0, R17.Pin_0, R18.Pin_0, R19.Pin_0
  N31: U2.Q0, LED9.anode
  N32: LED9.cathode, R19.Pin_1
  N33: LED10.cathode, R12.Pin_1
  N34: LED11.cathode, R13.Pin_1
  N35: LED12.cathode, R14.Pin_1
  N36: LED13.cathode, R15.Pin_1
  N37: LED14.cathode, R16.Pin_1
  N38: LED15.cathode, R17.Pin_1
  N39: LED16.cathode, R18.Pin_1

notes:
  D1-D2-D4-D5-D6-D7-RX-TX
  btn --- imput 1 to 8
  10kΩ NTC
