# Fritzing sketch supla_595_8x30 (saved by Fritzing 0.9.3b)
circuit board: 8.46667cm x 5.64444cm
breadboards: 1

parts:
  WeMos_D1_Mini1 = WeMos D1 Mini
  U1 = 74HC595 [part_number=1-8 package="DIP16 [THT]"]
  LED1 = smd LED [color="Red (633nm)" package="1206 [SMD]"]
  LED2 = smd LED [color="Red (633nm)" package="1206 [SMD]"]
  LED3 = smd LED [color="Red (633nm)" package="1206 [SMD]"]
  LED4 = smd LED [color="Red (633nm)" package="1206 [SMD]"]
  LED5 = smd LED [color="Red (633nm)" package="1206 [SMD]"]
  LED6 = smd LED [color="Red (633nm)" package="1206 [SMD]"]
  LED7 = smd LED [color="Red (633nm)" package="1206 [SMD]"]
  LED8 = smd LED [color="Red (633nm)" package="1206 [SMD]"]
  R9 = Resistor [tolerance=±5% resistance=220 package=THT]
  R2 = Resistor [tolerance=±5% resistance=220 package=THT]
  R3 = Resistor [tolerance=±5% resistance=220 package=THT]
  R4 = Resistor [tolerance=±5% resistance=220 package=THT]
  R5 = Resistor [tolerance=±5% resistance=220 package=THT]
  R6 = Resistor [tolerance=±5% resistance=220 package=THT]
  R7 = Resistor [tolerance=±5% resistance=220 package=THT]
  R8 = Resistor [tolerance=±5% resistance=220 package=THT]
  R10 = Temperature Sensor (Thermistor) [thermistor_type=NTC package=THT]
  R11 = Resistor [tolerance=±5% resistance=100k package="0603 [SMD]"]
  U2 = 74HC595 [part_number=9-16 package="DIP16 [THT]"]
  LED9 = smd LED [color="Red (633nm)" package="1206 [SMD]"]
  LED10 = smd LED [color="Red (633nm)" package="1206 [SMD]"]
  LED11 = smd LED [color="Red (633nm)" package="1206 [SMD]"]
  LED12 = smd LED [color="Red (633nm)" package="1206 [SMD]"]
  LED13 = smd LED [color="Red (633nm)" package="1206 [SMD]"]
  LED14 = smd LED [color="Red (633nm)" package="1206 [SMD]"]
  LED15 = smd LED [color="Red (633nm)" package="1206 [SMD]"]
  LED16 = smd LED [color="Red (633nm)" package="1206 [SMD]"]
  R12 = Resistor [tolerance=±5% resistance=220 package=THT]
  R13 = Resistor [tolerance=±5% resistance=220 package=THT]
  R14 = Resistor [tolerance=±5% resistance=220 package=THT]
  R15 = Resistor [tolerance=±5% resistance=220 package=THT]
  R16 = Resistor [tolerance=±5% resistance=220 package=THT]
  R17 = Resistor [tolerance=±5% resistance=220 package=THT]
  R18 = Resistor [tolerance=±5% resistance=220 package=THT]
  R19 = Resistor [tolerance=±5% resistance=220 package=THT]
  U3 = 74HC595 [part_number=9-16 package="DIP16 [THT]"]
  LED17 = smd LED [color="Red (633nm)" package="1206 [SMD]"]
  LED18 = smd LED [color="Red (633nm)" package="1206 [SMD]"]
  LED19 = smd LED [color="Red (633nm)" package="1206 [SMD]"]
  LED20 = smd LED [color="Red (633nm)" package="1206 [SMD]"]
  LED21 = smd LED [color="Red (633nm)" package="1206 [SMD]"]
  LED22 = smd LED [color="Red (633nm)" package="1206 [SMD]"]
  LED23 = smd LED [color="Red (633nm)" package="1206 [SMD]"]
  LED24 = smd LED [color="Red (633nm)" package="1206 [SMD]"]
  R20 = Resistor [tolerance=±5% resistance=220 package=THT]
  R21 = Resistor [tolerance=±5% resistance=220 package=THT]
  R22 = Resistor [tolerance=±5% resistance=220 package=THT]
  R23 = Resistor [tolerance=±5% resistance=220 package=THT]
  R24 = Resistor [tolerance=±5% resistance=220 package=THT]
  R25 = Resistor [tolerance=±5% resistance=220 package=THT]
  R26 = Resistor [tolerance=±5% resistance=220 package=THT]
  R27 = Resistor [tolerance=±5% resistance=220 package=THT]
  U4 = 74HC595 [part_number=9-16 package="DIP16 [THT]"]
  LED25 = smd LED [color="Red (633nm)" package="1206 [SMD]"]
  LED26 = smd LED [color="Red (633nm)" package="1206 [SMD]"]
  LED27 = smd LED [color="Red (633nm)" package="1206 [SMD]"]
  LED28 = smd LED [color="Red (633nm)" package="1206 [SMD]"]
  LED29 = smd LED [color="Red (633nm)" package="1206 [SMD]"]
  LED30 = smd LED [color="Red (633nm)" package="1206 [SMD]"]
  LED31 = smd LED [color="Red (633nm)" package="1206 [SMD]"]
  LED32 = smd LED [color="Red (633nm)" package="1206 [SMD]"]
  R28 = Resistor [tolerance=±5% resistance=220 package=THT]
  R29 = Resistor [tolerance=±5% resistance=220 package=THT]
  R30 = Resistor [tolerance=±5% resistance=220 package=THT]
  R31 = Resistor [tolerance=±5% resistance=220 package=THT]
  R32 = Resistor [tolerance=±5% resistance=220 package=THT]
  R33 = Resistor [tolerance=±5% resistance=220 package=THT]
  R34 = Resistor [tolerance=±5% resistance=220 package=THT]
  R35 = Resistor [tolerance=±5% resistance=220 package=THT]

nets:
  VCC: WeMos_D1_Mini1.3V3, U1.MR, U1.VCC, R11.Pin_0, U2.MR, U2.VCC
  N1: WeMos_D1_Mini1.A0, R10.pin_0, R11.Pin_1
  N2: WeMos_D1_Mini1.D0, U1.SH_CP, U2.SH_CP
  N3: WeMos_D1_Mini1.D3, U1.ST_CP, U2.ST_CP
  N4: WeMos_D1_Mini1.D8, U1.DS
  N5: WeMos_D1_Mini1.G, U1.GND, U1.OE, R9.Pin_0, R2.Pin_0, R3.Pin_0, R4.Pin_0, R5.Pin_0, R6.Pin_0, R7.Pin_0, R8.Pin_0, R10.pin_1
  N6: U1.Q1, LED1.anode
  N7: U1.Q2, LED2.anode
  N8: U1.Q3, LED3.anode
  N9: U1.Q4, LED4.anode
  N10: U1.Q5, LED5.anode
  N11: U1.Q6, LED6.anode
  N12: U1.Q7, LED7.anode
  N13: U1.Q7', U2.DS
  N14: U1.Q0, LED8.anode
  N15: LED1.cathode, R2.Pin_1
  N16: LED2.cathode, R3.Pin_1
  N17: LED3.cathode, R4.Pin_1
  N18: LED4.cathode, R5.Pin_1
  N19: LED5.cathode, R6.Pin_1
  N20: LED6.cathode, R7.Pin_1
  N21: LED7.cathode, R8.Pin_1
  N22: LED8.cathode, R9.Pin_1
  N23: U2.Q1, LED16.anode
  N24: U2.Q2, LED15.anode
  N25: U2.Q3, LED14.anode
  N26: U2.Q4, LED13.anode
  N27: U2.Q5, LED12.anode
  N28: U2.Q6, LED11.anode
  N29: U2.Q7, LED10.anode
  N30: U2.GND, U2.OE, R12.Pin_0, R13.Pin_0, R14.Pin_0, R15.Pin_0, R16.Pin_0, R17.Pin_0, R18.Pin_0, R19.Pin_0
  N31: U2.Q7', U3.DS
  N32: U2.Q0, LED9.anode
  N33: LED9.cathode, R19.Pin_1
  N34: LED10.cathode, R12.Pin_1
  N35: LED11.cathode, R13.Pin_1
  N36: LED12.cathode, R14.Pin_1
  N37: LED13.cathode, R15.Pin_1
  N38: LED14.cathode, R16.Pin_1
  N39: LED15.cathode, R17.Pin_1
  N40: LED16.cathode, R18.Pin_1
  N41: U3.Q1, LED24.anode
  N42: U3.Q2, LED23.anode
  N43: U3.Q3, LED22.anode
  N44: U3.Q4, LED21.anode
  N45: U3.Q5, LED20.anode
  N46: U3.Q6, LED19.anode
  N47: U3.Q7, LED18.anode
  N48: U3.GND, U3.OE, R20.Pin_0, R21.Pin_0, R22.Pin_0, R23.Pin_0, R24.Pin_0, R25.Pin_0, R26.Pin_0, R27.Pin_0
  N49: U3.Q7', U4.DS
  N50: U3.MR, U3.VCC
  N51: U3.SH_CP, U4.SH_CP
  N52: U3.ST_CP, U4.ST_CP
  N53: U3.Q0, LED17.anode
  N54: LED17.cathode, R27.Pin_1
  N55: LED18.cathode, R20.Pin_1
  N56: LED19.cathode, R21.Pin_1
  N57: LED20.cathode, R22.Pin_1
  N58: LED21.cathode, R23.Pin_1
  N59: LED22.cathode, R24.Pin_1
  N60: LED23.cathode, R25.Pin_1
  N61: LED24.cathode, R26.Pin_1
  N62: U4.Q1, LED32.anode
  N63: U4.Q2, LED31.anode
  N64: U4.Q3, LED30.anode
  N65: U4.Q4, LED29.anode
  N66: U4.Q5, LED28.anode
  N67: U4.Q6, LED27.anode
  N68: U4.Q7, LED26.anode
  N69: U4.GND, U4.OE, R28.Pin_0, R29.Pin_0, R30.Pin_0, R31.Pin_0, R32.Pin_0, R33.Pin_0, R34.Pin_0, R35.Pin_0
  N70: U4.MR, U4.VCC
  N71: U4.Q0, LED25.anode
  N72: LED25.cathode, R35.Pin_1
  N73: LED26.cathode, R28.Pin_1
  N74: LED27.cathode, R29.Pin_1
  N75: LED28.cathode, R30.Pin_1
  N76: LED29.cathode, R31.Pin_1
  N77: LED30.cathode, R32.Pin_1
  N78: LED31.cathode, R33.Pin_1
  N79: LED32.cathode, R34.Pin_1

notes:
  D1-D2-D4-D5-D6-D7-RX-TX
  btn --- imput 1 to 8
  10kΩ NTC
