# Fritzing sketch 8 canales analogico (saved by Fritzing 0.9.3b)

parts:
  U1 = 74HC4051 [package=so16]
  WeMos_D1_Mini1 = WeMos D1 Mini
  R1 = Resistor [tolerance=±5% resistance=180k package=THT]

nets:
  N1: U1.IO, R1.Pin_0
  N2: U1.INH, U1.VEE, U1.VSS, WeMos_D1_Mini1.G
  N3: U1.C, WeMos_D1_Mini1.D7
  N4: U1.B, WeMos_D1_Mini1.D6
  N5: U1.A, WeMos_D1_Mini1.D5
  VDD: U1.VDD, WeMos_D1_Mini1.5V
  N6: WeMos_D1_Mini1.A0, R1.Pin_1
