# Fritzing sketch aux_RF_board (saved by Fritzing 0.9.3b)
breadboards: 1

parts:
  WiFiConfig = Pushbutton [part_number=WiFiConfig package=THT]
  AT_0 = Pushbutton [package=THT]
  AT_1 = Pushbutton [package=THT]
  U1 = RF-LINK_RX [package=rf-link_rx]

nets:
  Gpio 0: WiFiConfig.leg0
  GND: WiFiConfig.leg1, AT_0.leg1, AT_1.leg1, U1.GND
  Gpio 5: AT_0.leg0
  Gpio4: AT_1.leg0
  Gpio 14: U1.DATA
  +3.3v: U1.+5V
