# Fritzing sketch conmutada (saved by Fritzing 0.9.3b)

parts:
  Part1 = KY-019 5V Relay Module [package="Breakout board"]
  S1 = Toggle Switch [package=THT]
  WeMos_D1_Mini1 = WeMos D1 Mini
  U1 = Sharp PC817 [package=THT]
  R1 = Resistor [tolerance=±5% resistance=150k package=THT]
  C1 = Electrolytic Capacitor [capacitance=1µF package="100 mil [THT, electrolytic]"]
  part = Resistor [tolerance=±5% resistance=10k package=THT]
  D1 = Rectifier Diode [package="Melf DO-213 AA [SMD]"]
  D2 = Rectifier Diode [package="Melf DO-213 AA [SMD]"]
  D3 = Rectifier Diode [package="Melf DO-213 AA [SMD]"]
  D4 = Rectifier Diode [package="Melf DO-213 AA [SMD]"]
  R2 = Resistor [tolerance=±5% resistance=220k package=THT]

nets:
  N1: Part1.S, WeMos_D1_Mini1.D2
  N2: Part1.+, WeMos_D1_Mini1.5V, part.Pin_0
  GND: Part1.-, WeMos_D1_Mini1.G, U1.Pin_3, C1.-
  N3: Part1.NC, S1.L2
  L out 220v AC: Part1.Common, D3.cathode, D4.anode
  N4: Part1.NO, S1.L1
  L in 220v AC: S1.COM
  N5: WeMos_D1_Mini1.D1, U1.Pin_4, C1.+, part.Pin_1
  N6: U1.Pin_1, R2.Pin_0
  N7: U1.Pin_2, D2.anode, D3.anode
  N8: R1.Pin_0, R2.Pin_1
  N9: R1.Pin_1, D1.cathode, D4.cathode
  Neutral: D1.anode, D2.cathode

custom parts:
  KY-019 5V Relay Module: KY-019 5V Relay module, used to control AC circuits.
