# Fritzing sketch 16x3.3v (saved by Fritzing 0.9.3b)
circuit board: 8.46667cm x 5.64444cm

parts:
  S16 = Pushbutton [package="[THT]"]
  R1 = Resistor [tolerance=±5% resistance=1k package=THT]
  R2 = Resistor [tolerance=±5% resistance=1k package=THT]
  R3 = Resistor [tolerance=±5% resistance=1k package=THT]
  R4 = Resistor [tolerance=±5% resistance=1k package=THT]
  R5 = Resistor [tolerance=±5% resistance=1k package=THT]
  R6 = Resistor [tolerance=±5% resistance=1k package=THT]
  R8 = Resistor [tolerance=±5% resistance=1k package=THT]
  S15 = Pushbutton [package="[THT]"]
  S14 = Pushbutton [package="[THT]"]
  S13 = Pushbutton [package="[THT]"]
  S12 = Pushbutton [package="[THT]"]
  S11 = Pushbutton [package="[THT]"]
  S10 = Pushbutton [package="[THT]"]
  S9 = Pushbutton [package="[THT]"]
  WeMos_D1_Mini1 = WeMos D1 Mini
  R7 = Resistor [tolerance=±5% resistance=1k package=THT]
  S6 = Momentary Switch [package=ksa_sealed_tac_switch]
  S5 = Momentary Switch [package=ksa_sealed_tac_switch]
  S4 = Momentary Switch [package=ksa_sealed_tac_switch]
  S3 = Momentary Switch [package=ksa_sealed_tac_switch]
  S2 = Momentary Switch [package=ksa_sealed_tac_switch]
  S1 = Momentary Switch [package=ksa_sealed_tac_switch]
  R9-16 = Resistor [tolerance=±5% resistance=4.7k package="2512 [SMD]"]
  R10 = Resistor [tolerance=±5% resistance=4.7k package="2512 [SMD]"]  # not connected
  R11 = Resistor [tolerance=±5% resistance=4.7k package="2512 [SMD]"]  # not connected
  R12 = Resistor [tolerance=±5% resistance=4.7k package="2512 [SMD]"]
  R13 = Resistor [tolerance=±5% resistance=4.7k package="2512 [SMD]"]
  R14 = Resistor [tolerance=±5% resistance=4.7k package="2512 [SMD]"]
  S8 = Momentary Switch [package=ksa_sealed_tac_switch]
  S7 = Momentary Switch [package=ksa_sealed_tac_switch]
  R15 = Resistor [tolerance=±5% resistance=4.7k package="2512 [SMD]"]
  R16 = Resistor [tolerance=±5% resistance=4.7k package="2512 [SMD]"]
  status_led = LED - 5mm [color="Red (633nm)" package="5 mm [THT]"]
  R17 = Resistor [tolerance=±5% resistance=220 package=THT]

nets:
  N1: S16.Pin_1, S16.Pin_2, R1.Pin_0, WeMos_D1_Mini1.3V3
  N2: S16.Pin_3, S16.Pin_4, S15.Pin_3, S15.Pin_4, S14.Pin_3, S14.Pin_4, S13.Pin_3, S13.Pin_4, S12.Pin_3, S12.Pin_4, S11.Pin_3, S11.Pin_4, S10.Pin_3, S10.Pin_4, S9.Pin_3, S9.Pin_4, WeMos_D1_Mini1.A0
  N3: R1.Pin_1, R2.Pin_0, S15.Pin_1, S15.Pin_2
  N4: R2.Pin_1, R3.Pin_0, S14.Pin_1, S14.Pin_2
  N5: R3.Pin_1, R4.Pin_0, S13.Pin_1, S13.Pin_2
  N6: R4.Pin_1, R5.Pin_0, S12.Pin_1, S12.Pin_2
  N7: R5.Pin_1, R6.Pin_0, S11.Pin_1, S11.Pin_2
  N8: R6.Pin_1, S10.Pin_1, S10.Pin_2, R7.Pin_0
  N9: R8.Pin_0, S9.Pin_1, S9.Pin_2, R7.Pin_1
  N10: R8.Pin_1, WeMos_D1_Mini1.G
  N11: WeMos_D1_Mini1.D0, S1.3
  N12: WeMos_D1_Mini1.D1, S2.3
  N13: WeMos_D1_Mini1.D2, S3.3
  N14: WeMos_D1_Mini1.D3, S4.3
  N15: WeMos_D1_Mini1.D4, S5.3
  N16: WeMos_D1_Mini1.D5, S6.2
  N17: WeMos_D1_Mini1.D6, S7.3
  N18: WeMos_D1_Mini1.D7, S8.2
  N19: WeMos_D1_Mini1.D8, R17.Pin_1
  N20: S6.1, R14.Pin_1
  N21: S6.3, S5.1
  N22: S6.4, S7.2
  N23: S5.2, S4.1
  N24: S5.4, R13.Pin_1
  N25: S4.2, S3.1
  N26: S4.4, R12.Pin_1
  N27: S3.2, S2.1
  N28: S2.2, S1.1
  N29: S1.2, status_led.cathode
  N30: S1.4, R9-16.Pin_1
  N31: S8.1, R16.Pin_1
  N32: S8.3, S7.1
  N33: S7.4, R15.Pin_1

notes:
  ADC = 3,3v wemos,
  nodemcu,etc...
