# Fritzing sketch 1.1v (saved by Fritzing 0.9.3b)
circuit board: 8.46667cm x 5.64444cm

parts:
  S8 = Pushbutton [package="[THT]"]
  R8 = Resistor [tolerance=±5% resistance=1k package=THT]
  R7 = Resistor [tolerance=±5% resistance=1k package=THT]
  R6 = Resistor [tolerance=±5% resistance=1k package=THT]
  R5 = Resistor [tolerance=±5% resistance=1k package=THT]
  R4 = Resistor [tolerance=±5% resistance=1k package=THT]
  R3 = Resistor [tolerance=±5% resistance=1k package=THT]
  R1 = Resistor [tolerance=±5% resistance=1k package=THT]
  S7 = Pushbutton [package="[THT]"]
  S6 = Pushbutton [package="[THT]"]
  S5 = Pushbutton [package="[THT]"]
  S4 = Pushbutton [package="[THT]"]
  S3 = Pushbutton [package="[THT]"]
  S2 = Pushbutton [package="[THT]"]
  S1 = Pushbutton [package="[THT]"]
  R2 = Resistor [tolerance=±5% resistance=1k package=THT]
  Componente1 = SparkFun ESP8266 Thing
  R9 = Resistor [tolerance=±5% resistance=220k package=THT]
  R10 = Resistor [tolerance=±5% resistance=100k package=THT]  # not connected

nets:
  N1: S8.Pin_1, S8.Pin_2, R8.Pin_0, Componente1.VCC
  N2: S8.Pin_3, S8.Pin_4, S7.Pin_3, S7.Pin_4, S6.Pin_3, S6.Pin_4, S5.Pin_3, S5.Pin_4, S4.Pin_3, S4.Pin_4, S3.Pin_3, S3.Pin_4, S2.Pin_3, S2.Pin_4, S1.Pin_3, S1.Pin_4, R9.Pin_0
  N3: R8.Pin_1, R7.Pin_0, S7.Pin_1, S7.Pin_2
  N4: R7.Pin_1, R6.Pin_0, S6.Pin_1, S6.Pin_2
  N5: R6.Pin_1, R5.Pin_0, S5.Pin_1, S5.Pin_2
  N6: R5.Pin_1, R4.Pin_0, S4.Pin_1, S4.Pin_2
  N7: R4.Pin_1, R3.Pin_0, S3.Pin_1, S3.Pin_2
  N8: R3.Pin_1, S2.Pin_1, S2.Pin_2, R2.Pin_0
  N9: R1.Pin_0, S1.Pin_1, S1.Pin_2, R2.Pin_1
  N10: R1.Pin_1, Componente1.GND
  N11: Componente1.ADC, R9.Pin_1

notes:
  ADC = 1,1 v
  esp12.etc...
  max 3,3v
  max 1,1v
