# Fritzing sketch 3.3v (saved by Fritzing 0.9.3b)
circuit board: 8.46667cm x 5.64444cm

parts:
  S8 = Pushbutton [package="[THT]"]
  part = Resistor [tolerance=±5% resistance=1k package=THT]
  part_2 = Resistor [tolerance=±5% resistance=1k package=THT]
  part_3 = Resistor [tolerance=±5% resistance=1k package=THT]
  part_4 = Resistor [tolerance=±5% resistance=1k package=THT]
  part_5 = Resistor [tolerance=±5% resistance=1k package=THT]
  part_6 = Resistor [tolerance=±5% resistance=1k package=THT]
  part_7 = Resistor [tolerance=±5% resistance=1k package=THT]
  S7 = Pushbutton [package="[THT]"]
  S6 = Pushbutton [package="[THT]"]
  S5 = Pushbutton [package="[THT]"]
  S4 = Pushbutton [package="[THT]"]
  S3 = Pushbutton [package="[THT]"]
  S2 = Pushbutton [package="[THT]"]
  S1 = Pushbutton [package="[THT]"]
  WeMos_D1_Mini1 = WeMos D1 Mini
  part_8 = Resistor [tolerance=±5% resistance=1k package=THT]

nets:
  N1: S8.Pin_1, S8.Pin_2, part.Pin_0, WeMos_D1_Mini1.3V3
  N2: S8.Pin_3, S8.Pin_4, S7.Pin_3, S7.Pin_4, S6.Pin_3, S6.Pin_4, S5.Pin_3, S5.Pin_4, S4.Pin_3, S4.Pin_4, S3.Pin_3, S3.Pin_4, S2.Pin_3, S2.Pin_4, S1.Pin_3, S1.Pin_4, WeMos_D1_Mini1.A0
  N3: part.Pin_1, part_2.Pin_0, S7.Pin_1, S7.Pin_2
  N4: part_2.Pin_1, part_3.Pin_0, S6.Pin_1, S6.Pin_2
  N5: part_3.Pin_1, part_4.Pin_0, S5.Pin_1, S5.Pin_2
  N6: part_4.Pin_1, part_5.Pin_0, S4.Pin_1, S4.Pin_2
  N7: part_5.Pin_1, part_6.Pin_0, S3.Pin_1, S3.Pin_2
  N8: part_6.Pin_1, S2.Pin_1, S2.Pin_2, part_8.Pin_0
  N9: part_7.Pin_0, S1.Pin_1, S1.Pin_2, part_8.Pin_1
  N10: part_7.Pin_1, WeMos_D1_Mini1.G

notes:
  ADC = 3,3v wemos,
  nodemcu,etc...
