# Fritzing sketch Untitled Sketch 2 (saved by Fritzing 0.9.3b)
circuit board: 8.46667cm x 5.64444cm
breadboards: 1

parts:
  U1 = ESP-12F (ESP8266 WiFi Module) [part_number=ESP8266]
  config = Pushbutton [package="[THT]"]
  L4 = Pushbutton [package="[THT]"]
  L3 = Pushbutton [package="[THT]"]
  L2 = Pushbutton [package="[THT]"]
  L1 = Pushbutton [package="[THT]"]
  part = Resistor [tolerance=±5% resistance=47k package=THT]
  part_2 = Resistor [tolerance=±5% resistance=47k package=THT]
  part_3 = Resistor [tolerance=±5% resistance=47k package=THT]
  part_4 = Resistor [tolerance=±5% resistance=47k package=THT]
  part_5 = Resistor [tolerance=±5% resistance=47k package=THT]
  D1 = Rectifier Diode [part_number=1N4001 package="300 mil [THT]"]
  D2 = Rectifier Diode [part_number=1N4001 package="300 mil [THT]"]
  D3 = Rectifier Diode [part_number=1N4001 package="300 mil [THT]"]
  D4 = Rectifier Diode [part_number=1N4001 package="300 mil [THT]"]
  D5 = Rectifier Diode [part_number=1N4001 package="300 mil [THT]"]
  part_6 = Resistor [tolerance=±5% resistance=10k package=THT]
  battery = DC Power [voltage=3.3V]
  D6 = Rectifier Diode [part_number=1N4001 package="300 mil [THT]"]
  part_7 = Resistor [tolerance=±5% resistance=12k package=THT]
  part_8 = Resistor [tolerance=±5% resistance=12k package=THT]
  Flash_Disable_Pullup = Resistor [tolerance=±5% resistance=220k package=THT]
  EN_to_VCC_for_programming = Reed switch [package=THT]

nets:
  N1: U1.VCC, U1.RST, config.Pin_3, config.Pin_4, L4.Pin_3, L4.Pin_4, L3.Pin_3, L3.Pin_4, L2.Pin_3, L2.Pin_4, L1.Pin_3, L1.Pin_4, battery.V+, part_8.Pin_1, Flash_Disable_Pullup.Pin_0, EN_to_VCC_for_programming.pin_1
  N2: U1.GPIO0, part_8.Pin_0
  N3: U1.EN, D1.cathode, D2.cathode, D3.cathode, D4.cathode, D5.cathode, part_6.Pin_1, D6.cathode, EN_to_VCC_for_programming.pin_2
  GND: U1.GND, part.Pin_0, part_2.Pin_0, part_3.Pin_0, part_4.Pin_0, part_5.Pin_0, part_6.Pin_0, battery.V-, part_7.Pin_0
  N4: U1.GPIO15, D6.anode, part_7.Pin_1
  N5: U1.GPIO4, L2.Pin_1, L2.Pin_2, part_2.Pin_1, D2.anode
  N6: U1.GPIO5, D1.anode
  N7: U1.GPIO14, L3.Pin_1, L3.Pin_2, part_3.Pin_1, D3.anode
  N8: U1.GPIO12, L4.Pin_1, L4.Pin_2, part_4.Pin_1, D4.anode
  N9: U1.GPIO13, config.Pin_1, config.Pin_2, part_5.Pin_1, D5.anode
  N10: U1.CS0, Flash_Disable_Pullup.Pin_1
  N11: L1.Pin_1, part.Pin_1

custom parts:
  ESP-12F (ESP8266 WiFi Module): WiFi Module based on the ESP8266 with onboard PCB antenna and UART communications
