# Fritzing sketch HC-SR501-Arduino (saved by Fritzing 0.9.3b)

parts:
  Sensore_PIR_HC-SR501 = HC-SR501 Body Sensor Module
  WeMos_D1_Mini1 = WeMos D1 Mini
  Wifi_config = Pushbutton [package="[THT]"]
  part = Resistor [tolerance=±5% resistance=4.7k package=THT]

nets:
  VCC: Sensore_PIR_HC-SR501.VCC, WeMos_D1_Mini1.5V
  N1: Sensore_PIR_HC-SR501.OUT, WeMos_D1_Mini1.D6, part.Pin_1
  N2: Sensore_PIR_HC-SR501.GND, WeMos_D1_Mini1.G, Wifi_config.Pin_3, Wifi_config.Pin_4, part.Pin_0
  N3: WeMos_D1_Mini1.D3, Wifi_config.Pin_1, Wifi_config.Pin_2

custom parts:
  HC-SR501 Body Sensor Module: Pyroelectric Infrared PIR Motion Sensor Detector Module
