# Fritzing sketch thermostat_Remote_oled (saved by Fritzing 0.9.3b)

parts:
  WeMos_D1_Mini1 = WeMos D1 Mini
  SSD1306/SH1106 = Module display OLED I2C 128x64 SSD1306 [package=THT]
  aut_/_man = Pushbutton [package="[THT]"]
  on/off = Pushbutton [package="[THT]"]
  -0_5º = Pushbutton [package="[THT]"]
  +0_5º = Pushbutton [package="[THT]"]

nets:
  3V3: WeMos_D1_Mini1.3V3, SSD1306/SH1106.VCC
  N1: WeMos_D1_Mini1.D1, -0_5º.Pin_1, -0_5º.Pin_2
  N2: WeMos_D1_Mini1.D2, +0_5º.Pin_1, +0_5º.Pin_2
  N3: WeMos_D1_Mini1.D3, SSD1306/SH1106.SDA
  N4: WeMos_D1_Mini1.D4, SSD1306/SH1106.SCL
  N5: WeMos_D1_Mini1.D5, on/off.Pin_4
  N6: WeMos_D1_Mini1.D6, aut_/_man.Pin_4
  N7: SSD1306/SH1106.GND, aut_/_man.Pin_1, aut_/_man.Pin_2
  N8: on/off.Pin_1, on/off.Pin_2, -0_5º.Pin_3, -0_5º.Pin_4, +0_5º.Pin_3

custom parts:
  Module display OLED I2C 128x64 SSD1306: Ecran OLED I2C SSD163 de 128x64 avec connexion I2C
