# Fritzing sketch lcd_i2c (1) (saved by Fritzing 0.9.3b)

parts:
  U4 = LCD-16X2 [package=lcd-16x2_noholes]
  WeMos_D1_Mini1 = WeMos D1 Mini
  S1 = Momentary Switch [package=ksa_sealed_tac_switch]
  S2 = Momentary Switch [package=ksa_sealed_tac_switch]
  S3 = Momentary Switch [package=ksa_sealed_tac_switch]
  S4 = Momentary Switch [package=ksa_sealed_tac_switch]
  S5 = Momentary Switch [package=ksa_sealed_tac_switch]
  S6 = Momentary Switch [package=ksa_sealed_tac_switch]
  R1 = Resistor [tolerance=±5% resistance=4.7k package="2512 [SMD]"]
  R2 = Resistor [tolerance=±5% resistance=4.7k package="2512 [SMD]"]
  R3 = Resistor [tolerance=±5% resistance=4.7k package="2512 [SMD]"]
  R4 = Resistor [tolerance=±5% resistance=4.7k package="2512 [SMD]"]  # not connected
  R5 = Resistor [tolerance=±5% resistance=4.7k package="2512 [SMD]"]  # not connected
  R1-R6 = Resistor [tolerance=±5% resistance=4.7k package="2512 [SMD]"]
  S7 = Pushbutton [package="[THT]"]
  S8 = Pushbutton [package="[THT]"]
  S9 = Pushbutton [package="[THT]"]
  S10 = Pushbutton [package="[THT]"]
  S11 = Pushbutton [package="[THT]"]
  S12 = Pushbutton [package="[THT]"]
  S13 = Pushbutton [package="[THT]"]
  S14 = Pushbutton [package="[THT]"]
  R8 = Resistor [tolerance=±5% resistance=1k package=THT]
  R7 = Resistor [tolerance=±5% resistance=1k package=THT]
  R9 = Resistor [tolerance=±5% resistance=1k package=THT]
  R10 = Resistor [tolerance=±5% resistance=1k package=THT]
  R11 = Resistor [tolerance=±5% resistance=1k package=THT]
  R12 = Resistor [tolerance=±5% resistance=1k package=THT]
  R13 = Resistor [tolerance=±5% resistance=1k package=THT]
  R14 = Resistor [tolerance=±5% resistance=1k package=THT]

nets:
  N1: U4.VSS, S5.2, S6.1, R7.Pin_1
  VDD: U4.VDD, U4.VO, WeMos_D1_Mini1.5V
  N2: U4.A, WeMos_D1_Mini1.D2
  N3: U4.K, WeMos_D1_Mini1.D1
  N4: WeMos_D1_Mini1.3V3, R1.Pin_0, R2.Pin_0, R1-R6.Pin_0, S14.Pin_1, S14.Pin_2, R14.Pin_0
  N5: WeMos_D1_Mini1.A0, S7.Pin_3, S7.Pin_4, S8.Pin_3, S8.Pin_4, S9.Pin_3, S9.Pin_4, S10.Pin_3, S10.Pin_4, S11.Pin_3, S11.Pin_4, S12.Pin_3, S12.Pin_4, S13.Pin_3, S13.Pin_4, S14.Pin_3, S14.Pin_4
  N6: WeMos_D1_Mini1.D0, S1.2
  N7: WeMos_D1_Mini1.D3, S2.3
  N8: WeMos_D1_Mini1.D4, S3.3
  N9: WeMos_D1_Mini1.D5, S4.3
  N10: WeMos_D1_Mini1.D6, S5.3
  N11: WeMos_D1_Mini1.D7, S6.3
  N12: WeMos_D1_Mini1.G, S1.4
  N13: S1.1, R1.Pin_1
  N14: S1.3, S2.1
  N15: S2.2, S3.1
  N16: S2.4, R2.Pin_1
  N17: S3.2, S4.1
  N18: S3.4, R3.Pin_1
  N19: S4.2, S5.1
  N20: S6.4, R1-R6.Pin_1
  N21: S7.Pin_2, R8.Pin_1, R7.Pin_0
  N22: S8.Pin_1, S8.Pin_2, R8.Pin_0, R9.Pin_1
  N23: S9.Pin_1, S9.Pin_2, R9.Pin_0, R10.Pin_1
  N24: S10.Pin_1, S10.Pin_2, R10.Pin_0, R11.Pin_1
  N25: S11.Pin_1, S11.Pin_2, R11.Pin_0, R12.Pin_1
  N26: S12.Pin_1, S12.Pin_2, R12.Pin_0, R13.Pin_1
  N27: S13.Pin_1, S13.Pin_2, R13.Pin_0, R14.Pin_1
