# Fritzing sketch irControler (saved by Fritzing 0.9.3b)

parts:
  WeMos_D1_Mini1 = WeMos D1 Mini
  part = LED - 5mm [color="Infrared (940nm)" package="5 mm [THT]"]
  part_2 = Resistor [tolerance=±5% resistance=10 package=THT]
  Q1 = NPN-Transistor [package="TO92 [THT]"]
  part_3 = Resistor [tolerance=±5% resistance=1k package=THT]
  part_4 = Resistor [tolerance=±5% resistance=100 package=THT]
  IR1 = TSOP312.., 314.. [package=THT]
  part_5 = Electrolytic Capacitor [capacitance=10µF package="100 mil [THT, electrolytic]"]
  WiFiConfig = Pushbutton [package=THT]

nets:
  N1: WeMos_D1_Mini1.3V3, part_4.Pin_1
  N2: WeMos_D1_Mini1.5V, part_2.Pin_0
  N3: WeMos_D1_Mini1.D2, part_3.Pin_0
  N4: WeMos_D1_Mini1.D3, WiFiConfig.leg1
  N5: WeMos_D1_Mini1.D5, IR1.Data
  N6: WeMos_D1_Mini1.G, Q1.E, IR1.GND, part_5.-, WiFiConfig.leg0
  N7: part.cathode, Q1.C
  N8: part.anode, part_2.Pin_1
  N9: Q1.B, part_3.Pin_1
  N10: part_4.Pin_0, IR1.Vs, part_5.+
