# Fritzing sketch Untitled Sketch (saved by Fritzing 0.9.3b)

parts:
  WeMos_D1_Mini1 = WeMos D1 Mini
  config = Pushbutton [package="[THT]"]
  sensor = Camdenboss CTB0158-2 [part_number=CTB0158-2 package=THT]
  part = Resistor [tolerance=±5% resistance=1k package=THT]
  part_2 = TP4056 [chip_label=TP4056 package="DIP (Dual Inline) [THT]"]
  part_3 = Rectifier Diode [part_number=1N4001 package="300 mil [THT]"]
  BAT1 = 18650 battery holder [package=battery-18650-kit]

nets:
  N1: WeMos_D1_Mini1.3V3, part_3.cathode
  N2: WeMos_D1_Mini1.D0, part.Pin_0
  N3: WeMos_D1_Mini1.D5, config.Pin_4
  N4: WeMos_D1_Mini1.D6, sensor.pin1
  N5: WeMos_D1_Mini1.G, config.Pin_1, config.Pin_2, sensor.pin2, part_2.pin6
  N6: WeMos_D1_Mini1.RST, part.Pin_1
  N7: part_2.pin3, part_3.anode
  N8: part_2.pin4, BAT1.+
  N9: part_2.pin5, BAT1.-

custom parts:
  TP4056: A DIP stand-in part for whatever IC you want. With 6 pins on a 300mil dual inline package (DIP) footprint.
  18650 battery holder: 18650 Battery Holder
