# Fritzing sketch low power bme 280 (saved by Fritzing 0.9.3b)

parts:
  WeMos_D1_Mini1 = WeMos D1 Mini
  config = Pushbutton [package="[THT]"]
  sensor = Camdenboss CTB0158-2 [part_number=CTB0158-2 package=THT]
  R1 = Resistor [tolerance=±5% resistance=1k package=THT]
  TP1 = TP4056 [chip_label=TP4056 package="DIP (Dual Inline) [THT]"]
  D1 = Rectifier Diode [part_number=1N4001 package="300 mil [THT]"]
  BAT1 = 18650 battery holder [package=battery-18650-kit]
  Componente1 = BME280 Breakout

nets:
  N1: WeMos_D1_Mini1.3V3, D1.cathode
  N2: WeMos_D1_Mini1.D0, R1.Pin_0
  N3: WeMos_D1_Mini1.D1, Componente1.SCK/SCL
  N4: WeMos_D1_Mini1.D2, Componente1.SDI/SDA
  N5: WeMos_D1_Mini1.D5, config.Pin_4
  N6: WeMos_D1_Mini1.D6, sensor.pin1
  N7: WeMos_D1_Mini1.D7, Componente1.3.3V
  N8: WeMos_D1_Mini1.G, config.Pin_1, config.Pin_2, sensor.pin2, TP1.pin6
  N9: WeMos_D1_Mini1.RST, R1.Pin_1
  N10: TP1.pin3, D1.anode
  N11: TP1.pin4, BAT1.+
  N12: TP1.pin5, BAT1.-

custom parts:
  TP4056: A DIP stand-in part for whatever IC you want. With 6 pins on a 300mil dual inline package (DIP) footprint.
  18650 battery holder: 18650 Battery Holder
