# Fritzing sketch supla_8P_16B (saved by Fritzing 0.9.3b)

parts:
  MCP23017_relays = CJMCU2317-MCP23017
  8_Channel_Relay_active_high = 8 Channel Power Relay
  WeMos_D1_Mini1 = WeMos D1 Mini
  motor0 = JST-VHR-3N [part_number=JST-VHR-3N package=THT]
  8_Channel_Relay_active_high_2 = 8 Channel Power Relay
  MCP23017_buttons = CJMCU2317-MCP23017
  B2_2UP = Pushbutton [package="[THT]"]
  B3_3UP = Pushbutton [package="[THT]"]
  B4_4UP = Pushbutton [package="[THT]"]
  B5_5UP = Pushbutton [package="[THT]"]
  B6_6UP = Pushbutton [package="[THT]"]
  B7_7UP = Pushbutton [package="[THT]"]
  B0_0UP = Pushbutton [package="[THT]"]
  B1_1UP = Pushbutton [package="[THT]"]
  A2_2DOWN = Pushbutton [package="[THT]"]
  A0_0DOWN = Pushbutton [package="[THT]"]
  A4_4DOWN = Pushbutton [package="[THT]"]
  A6_6DOWN = Pushbutton [package="[THT]"]
  A3_3DOWN = Pushbutton [package="[THT]"]
  A1_1DOWN = Pushbutton [package="[THT]"]
  A5_5DOWN = Pushbutton [package="[THT]"]
  A7_7DOWN = Pushbutton [package="[THT]"]
  WiFiConfig = Pushbutton [package="[THT]"]
  motor1 = JST-VHR-3N [part_number=JST-VHR-3N package=THT]
  motor2 = JST-VHR-3N [part_number=JST-VHR-3N package=THT]
  motor3 = JST-VHR-3N [part_number=JST-VHR-3N package=THT]
  220v_in = JST-VHR-3N [part_number=JST-VHR-3N package=THT]
  motor4 = JST-VHR-3N [part_number=JST-VHR-3N package=THT]
  motor5 = JST-VHR-3N [part_number=JST-VHR-3N package=THT]
  motor6 = JST-VHR-3N [part_number=JST-VHR-3N package=THT]
  motor7 = JST-VHR-3N [part_number=JST-VHR-3N package=THT]
  220v_in_2 = JST-VHR-3N [part_number=JST-VHR-3N package=THT]
  Status_Led = LED - 5mm [color="Red (633nm)" package="5 mm [THT]"]
  R1 = Resistor [tolerance=±5% resistance=100 package=THT]  # not connected

nets:
  N1: MCP23017_relays.SDA/SDI/SDO, WeMos_D1_Mini1.D2, MCP23017_buttons.SDA/SDI/SDO
  N2: MCP23017_relays.SCL/SCLK, WeMos_D1_Mini1.D1, MCP23017_buttons.SCL/SCLK
  GND: MCP23017_relays.GND, MCP23017_relays.ADDR2, MCP23017_relays.ADDR1, MCP23017_relays.ADDR0, 8_Channel_Relay_active_high.GND, WeMos_D1_Mini1.G, 8_Channel_Relay_active_high_2.GND, MCP23017_buttons.GND#16, MCP23017_buttons.ADDR2, MCP23017_buttons.ADDR1, WiFiConfig.Pin_1
  VCC: MCP23017_relays.VCC, WeMos_D1_Mini1.3V3, MCP23017_buttons.VCC, MCP23017_buttons.ADDR0
  N3: MCP23017_relays.RESET, WeMos_D1_Mini1.D4, MCP23017_buttons.RESET
  N4: MCP23017_relays.GPB0, 8_Channel_Relay_active_high.IN2
  N5: MCP23017_relays.GPB1, 8_Channel_Relay_active_high.IN4
  N6: MCP23017_relays.GPB2, 8_Channel_Relay_active_high.IN6
  N7: MCP23017_relays.GPB3, 8_Channel_Relay_active_high.IN8
  N8: MCP23017_relays.GPB4, 8_Channel_Relay_active_high_2.IN2
  N9: MCP23017_relays.GPB5, 8_Channel_Relay_active_high_2.IN4
  N10: MCP23017_relays.GPB6, 8_Channel_Relay_active_high_2.IN6
  N11: MCP23017_relays.GPB7, 8_Channel_Relay_active_high_2.IN8
  N12: MCP23017_relays.GPA0, 8_Channel_Relay_active_high.IN1
  N13: MCP23017_relays.GPA1, 8_Channel_Relay_active_high.IN3
  N14: MCP23017_relays.GPA2, 8_Channel_Relay_active_high.IN5
  N15: MCP23017_relays.GPA3, 8_Channel_Relay_active_high.IN7
  N16: MCP23017_relays.GPA4, 8_Channel_Relay_active_high_2.IN1
  N17: MCP23017_relays.GPA5, 8_Channel_Relay_active_high_2.IN3
  N18: MCP23017_relays.GPA6, 8_Channel_Relay_active_high_2.IN5
  N19: MCP23017_relays.GPA7, 8_Channel_Relay_active_high_2.IN7
  VCC_2: 8_Channel_Relay_active_high.VCC, WeMos_D1_Mini1.5V, 8_Channel_Relay_active_high_2.VCC
  N20: 8_Channel_Relay_active_high.COM#22, 8_Channel_Relay_active_high.NC#24
  N21: 8_Channel_Relay_active_high.NO#23, motor0.pin1, motor0.pin_4
  N22: 8_Channel_Relay_active_high.COM#25, 8_Channel_Relay_active_high.COM#31, 8_Channel_Relay_active_high.COM#37, 8_Channel_Relay_active_high.COM#43, 220v_in.pin1, 220v_in.pin_4
  N23: 8_Channel_Relay_active_high.NO#26, motor0.pin3, motor0.pin_6
  N24: 8_Channel_Relay_active_high.COM#28, 8_Channel_Relay_active_high.NC#30
  N25: 8_Channel_Relay_active_high.NO#29, motor1.pin1, motor1.pin_4
  N26: 8_Channel_Relay_active_high.NO#32, motor1.pin3, motor1.pin_6
  N27: 8_Channel_Relay_active_high.COM#34, 8_Channel_Relay_active_high.NC#36
  N28: 8_Channel_Relay_active_high.NO#35, motor2.pin1, motor2.pin_4
  N29: 8_Channel_Relay_active_high.NO#38, motor2.pin3, motor2.pin_6
  N30: 8_Channel_Relay_active_high.COM#40, 8_Channel_Relay_active_high.NC#42
  N31: 8_Channel_Relay_active_high.NO#41, motor3.pin1, motor3.pin_4
  N32: 8_Channel_Relay_active_high.NO#44, motor3.pin3, motor3.pin_6
  N33: WeMos_D1_Mini1.D0, Status_Led.anode
  N34: WeMos_D1_Mini1.D3, WiFiConfig.Pin_3, WiFiConfig.Pin_4
  N35: motor0.pin_5, motor1.pin_5, motor2.pin_5, motor3.pin_5, 220v_in.pin3, 220v_in.pin_6
  N36: 8_Channel_Relay_active_high_2.COM#22, 8_Channel_Relay_active_high_2.NC#24
  N37: 8_Channel_Relay_active_high_2.NO#23, motor4.pin_4
  N38: 8_Channel_Relay_active_high_2.COM#25, 8_Channel_Relay_active_high_2.COM#31, 8_Channel_Relay_active_high_2.COM#37, 8_Channel_Relay_active_high_2.COM#43, 220v_in_2.pin_4
  N39: 8_Channel_Relay_active_high_2.NO#26, motor4.pin_6
  N40: 8_Channel_Relay_active_high_2.COM#28, 8_Channel_Relay_active_high_2.NC#30
  N41: 8_Channel_Relay_active_high_2.NO#29, motor5.pin_4
  N42: 8_Channel_Relay_active_high_2.NO#32, motor5.pin_6
  N43: 8_Channel_Relay_active_high_2.COM#34, 8_Channel_Relay_active_high_2.NC#36
  N44: 8_Channel_Relay_active_high_2.NO#35, motor6.pin_4
  N45: 8_Channel_Relay_active_high_2.NO#38, motor6.pin_6
  N46: 8_Channel_Relay_active_high_2.COM#40, 8_Channel_Relay_active_high_2.NC#42
  N47: 8_Channel_Relay_active_high_2.NO#41, motor7.pin_4
  N48: 8_Channel_Relay_active_high_2.NO#44, motor7.pin_6
  N49: MCP23017_buttons.GPB0, B0_0UP.Pin_3
  N50: MCP23017_buttons.GPB1, B1_1UP.Pin_3
  N51: MCP23017_buttons.GPB2, B2_2UP.Pin_3
  N52: MCP23017_buttons.GPB3, B3_3UP.Pin_3
  N53: MCP23017_buttons.GPB4, B4_4UP.Pin_3
  N54: MCP23017_buttons.GPB5, B5_5UP.Pin_3, B5_5UP.Pin_4
  N55: MCP23017_buttons.GPB6, B6_6UP.Pin_3, B6_6UP.Pin_4
  N56: MCP23017_buttons.GPB7, B7_7UP.Pin_3, B7_7UP.Pin_4
  N57: MCP23017_buttons.GPA0, A0_0DOWN.Pin_1
  N58: MCP23017_buttons.GPA1, A1_1DOWN.Pin_1, A1_1DOWN.Pin_2
  N59: MCP23017_buttons.GPA2, A2_2DOWN.Pin_1, A2_2DOWN.Pin_2
  N60: MCP23017_buttons.GPA3, A3_3DOWN.Pin_1, A3_3DOWN.Pin_2
  N61: MCP23017_buttons.GPA4, A4_4DOWN.Pin_1, A4_4DOWN.Pin_2
  N62: MCP23017_buttons.GPA5, A5_5DOWN.Pin_1, A5_5DOWN.Pin_2
  N63: MCP23017_buttons.GPA6, A6_6DOWN.Pin_1, A6_6DOWN.Pin_2
  N64: MCP23017_buttons.GPA7, A7_7DOWN.Pin_1, A7_7DOWN.Pin_2
  N65: MCP23017_buttons.GND#41, B2_2UP.Pin_1, B2_2UP.Pin_2, B3_3UP.Pin_1, B3_3UP.Pin_2, B4_4UP.Pin_1, B4_4UP.Pin_2, B5_5UP.Pin_1, B5_5UP.Pin_2, B6_6UP.Pin_1, B6_6UP.Pin_2, B7_7UP.Pin_2, B0_0UP.Pin_1, B0_0UP.Pin_2, B1_1UP.Pin_1, B1_1UP.Pin_2, A2_2DOWN.Pin_3, A2_2DOWN.Pin_4, A0_0DOWN.Pin_3, A0_0DOWN.Pin_4, A4_4DOWN.Pin_3, A4_4DOWN.Pin_4, A6_6DOWN.Pin_3, A6_6DOWN.Pin_4, A3_3DOWN.Pin_3, A3_3DOWN.Pin_4, A1_1DOWN.Pin_3, A1_1DOWN.Pin_4, A5_5DOWN.Pin_3, A5_5DOWN.Pin_4, A7_7DOWN.Pin_4
  N66: motor4.pin_5, motor5.pin_5, motor6.pin_5, motor7.pin_5, 220v_in_2.pin3, 220v_in_2.pin_6

notes:
  Brown Shut
  Gray Reveal

custom parts:
  CJMCU2317-MCP23017: The MCP23017 device family provides 16-bit, general purpose parallel I/O expansion for I2C bus. The MCP23X17 consists of multiple 8-bit configuration registers for input, output and polarity selection. The system master can enable the I/Os as either inputs or outputs by writing the I/O configuration bits (IODIRA/B). The data for each input or output is kept in the corresponding input or output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
  8 Channel Power Relay: An 8 channel power relay. The module operates at 5V.
