# Fritzing sketch R2 (saved by Fritzing 0.9.3b)
breadboards: 1

parts:
  U1 = NodeMCU V3.0
  IC1 = 24LC32 [package=THT]
  U2 = RELAY [package=relay-g5q]
  D1 = Rectifier Diode [part_number=1N4001 package="300 mil [THT]"]
  Q1 = NPN-Transistor [package="TO92 [THT]"]
  R1 = Resistor [tolerance=±5% resistance=1k package=THT]
  U3 = RELAY [package=relay-g5q]
  D2 = Rectifier Diode [part_number=1N4001 package="300 mil [THT]"]
  Q2 = NPN-Transistor [package="TO92 [THT]"]
  R2 = Resistor [tolerance=±5% resistance=1k package=THT]
  U4 = RELAY [package=relay-g5q]
  D3 = Rectifier Diode [part_number=1N4001 package="300 mil [THT]"]
  Q3 = NPN-Transistor [package="TO92 [THT]"]
  R3 = Resistor [tolerance=±5% resistance=1k package=THT]
  U5 = RELAY [package=relay-g5q]
  D4 = Rectifier Diode [part_number=1N4001 package="300 mil [THT]"]
  Q4 = NPN-Transistor [package="TO92 [THT]"]
  R4 = Resistor [tolerance=±5% resistance=1k package=THT]
  S1 = Pushbutton [package=THT]
  S2 = Pushbutton [package=THT]
  S3 = Pushbutton [package=THT]
  S4 = Pushbutton [package=THT]
  LED1 = LED - 5mm [color="Red (633nm)" package="5 mm [THT]"]
  R5 = Resistor [tolerance=±5% resistance=220 package=THT]

nets:
  N1: U1.D0, R5.Pin_1
  N2: U1.D1, R1.Pin_0
  N3: U1.D2, R2.Pin_0
  N4: U1.D3, IC1.SDA_-_I2C_Data
  N5: U1.D4, IC1.SCL_-_I2C_Clock
  N6: U1.3V3, IC1.+V, LED1.anode
  GND: U1.GND, IC1.A0, IC1.A1, IC1.A2, IC1.0V, IC1.WP_-_Write_Protect, Q1.E, Q2.E, Q3.E, Q4.E, S1.leg0, S2.leg0, S3.leg0, S4.leg0
  N7: U1.D5, R3.Pin_0
  N8: U1.D6, R4.Pin_0
  N9: U1.D7, S4.leg1
  N10: U1.D8, S3.leg1
  N11: U1.RX, S2.leg1
  5V: U1.Vin, U2.COIL1, D1.cathode, U3.COIL1, D2.cathode, U4.COIL1, D3.cathode, U5.COIL1, D4.cathode
  N12: U1.S2, S1.leg1
  N13: U2.COIL2, D1.anode, Q1.C
  N14: Q1.B, R1.Pin_1
  N15: U3.COIL2, D2.anode, Q2.C
  N16: Q2.B, R2.Pin_1
  N17: U4.COIL2, D3.anode, Q3.C
  N18: Q3.B, R3.Pin_1
  N19: U5.COIL2, D4.anode, Q4.C
  N20: Q4.B, R4.Pin_1
  N21: LED1.cathode, R5.Pin_0

custom parts:
  NodeMCU V3.0: ESP8266 based NodeMCU
