# Fritzing sketch Untitled Sketch (saved by Fritzing 0.9.3b)

parts:
  MCP23017 = CJMCU2317-MCP23017
  8_Channel_Relay_active_high = 8 Channel Power Relay
  WeMos_D1_Mini1 = WeMos D1 Mini
  sensor1 = Reed switch [package=THT]
  sensor2 = Reed switch [package=THT]
  sensor3 = Reed switch [package=THT]
  sensor4 = Reed switch [package=THT]
  1up = Momentary Switch [package=ksa_sealed_tac_switch]
  1do = Momentary Switch [package=ksa_sealed_tac_switch]
  2up = Momentary Switch [package=ksa_sealed_tac_switch]
  2do = Momentary Switch [package=ksa_sealed_tac_switch]
  3up = Momentary Switch [package=ksa_sealed_tac_switch]
  3do = Momentary Switch [package=ksa_sealed_tac_switch]
  4up = Momentary Switch [package=ksa_sealed_tac_switch]
  4do = Momentary Switch [package=ksa_sealed_tac_switch]
  motor = JST-VHR-3N [part_number=JST-VHR-3N package=THT]
  220v_in = JST-VHR-3N [part_number=JST-VHR-3N package=THT]
  status_led = LED - 5mm [color="Red (633nm)" package="5 mm [THT]"]
  part = Resistor [tolerance=±5% resistance=220 package=THT]

nets:
  N1: MCP23017.SDA/SDI/SDO, WeMos_D1_Mini1.D2
  N2: MCP23017.SCL/SCLK, WeMos_D1_Mini1.D1
  GND: MCP23017.GND, MCP23017.ADDR2, MCP23017.ADDR1, MCP23017.ADDR0, 8_Channel_Relay_active_high.GND, WeMos_D1_Mini1.G, sensor1.pin_1, sensor2.pin_1, sensor3.pin_1, sensor4.pin_1, 1up.3, 4do.1, 4do.2, status_led.anode
  VCC: MCP23017.VCC, WeMos_D1_Mini1.3V3
  N3: MCP23017.GPB0, 1up.2
  N4: MCP23017.GPB1, 1do.2
  N5: MCP23017.GPB2, 2up.2
  N6: MCP23017.GPB3, 2do.2
  N7: MCP23017.GPB4, 3up.4
  N8: MCP23017.GPB5, 3do.4
  N9: MCP23017.GPB6, 4up.4
  N10: MCP23017.GPB7, 4do.4
  N11: MCP23017.GPA0, 8_Channel_Relay_active_high.IN1
  N12: MCP23017.GPA1, 8_Channel_Relay_active_high.IN2
  N13: MCP23017.GPA2, 8_Channel_Relay_active_high.IN3
  N14: MCP23017.GPA3, 8_Channel_Relay_active_high.IN4
  N15: MCP23017.GPA4, 8_Channel_Relay_active_high.IN5
  N16: MCP23017.GPA5, 8_Channel_Relay_active_high.IN6
  N17: MCP23017.GPA6, 8_Channel_Relay_active_high.IN7
  N18: MCP23017.GPA7, 8_Channel_Relay_active_high.IN8
  VCC_2: 8_Channel_Relay_active_high.VCC, WeMos_D1_Mini1.5V
  N19: 8_Channel_Relay_active_high.COM#22, 8_Channel_Relay_active_high.NC
  N20: 8_Channel_Relay_active_high.NO#23, motor.pin1, motor.pin_4
  N21: 8_Channel_Relay_active_high.COM#25, 220v_in.pin3, 220v_in.pin_6
  N22: 8_Channel_Relay_active_high.NO#26, motor.pin3, motor.pin_6
  N23: WeMos_D1_Mini1.D0, part.Pin_1
  N24: WeMos_D1_Mini1.D4, sensor1.pin_2
  N25: WeMos_D1_Mini1.D5, sensor2.pin_2
  N26: WeMos_D1_Mini1.D6, sensor3.pin_2
  N27: WeMos_D1_Mini1.D7, sensor4.pin_2
  N28: motor.pin_5, 220v_in.pin2, 220v_in.pin_5

custom parts:
  CJMCU2317-MCP23017: The MCP23017 device family provides 16-bit, general purpose parallel I/O expansion for I2C bus. The MCP23X17 consists of multiple 8-bit configuration registers for input, output and polarity selection. The system master can enable the I/Os as either inputs or outputs by writing the I/O configuration bits (IODIRA/B). The data for each input or output is kept in the corresponding input or output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
  8 Channel Power Relay: An 8 channel power relay. The module operates at 5V.
