# Fritzing sketch Untitled Sketch (saved by Fritzing 0.9.3b)

parts:
  CJMCU2317 = CJMCU2317-MCP23017
  8_Channel_Relay_active_high = 8 Channel Power Relay
  WeMos_D1_Mini1 = WeMos D1 Mini
  sensor1 = Reed switch [package=THT]
  sensor2 = Reed switch [package=THT]
  sensor3 = Reed switch [package=THT]
  sensor4 = Reed switch [package=THT]
  1up = Momentary Switch [package=ksa_sealed_tac_switch]
  1do = Momentary Switch [package=ksa_sealed_tac_switch]
  2up = Momentary Switch [package=ksa_sealed_tac_switch]
  2do = Momentary Switch [package=ksa_sealed_tac_switch]
  3up = Momentary Switch [package=ksa_sealed_tac_switch]
  3do = Momentary Switch [package=ksa_sealed_tac_switch]
  4up = Momentary Switch [package=ksa_sealed_tac_switch]
  4do = Momentary Switch [package=ksa_sealed_tac_switch]
  motor = JST-VHR-3N [part_number=JST-VHR-3N package=THT]
  220v_in = JST-VHR-3N [part_number=JST-VHR-3N package=THT]
  status_led = LED - 5mm [color="Red (633nm)" package="5 mm [THT]"]  # not connected
  part = Resistor [tolerance=±5% resistance=220 package=THT]
  10k = Temperature Sensor (Thermistor) [thermistor_type=NTC package=THT]  # not connected
  part_2 = Resistor [tolerance=±5% resistance=100k package=THT]
  24c32 = 24LC32 [package=THT]

nets:
  N1: CJMCU2317.SDA/SDI/SDO, WeMos_D1_Mini1.D2, 24c32.SDA_-_I2C_Data
  N2: CJMCU2317.SCL/SCLK, WeMos_D1_Mini1.D1, 24c32.SCL_-_I2C_Clock
  GND: CJMCU2317.GND, CJMCU2317.ADDR2, CJMCU2317.ADDR1, CJMCU2317.ADDR0, 8_Channel_Relay_active_high.GND, WeMos_D1_Mini1.G, sensor1.pin_1, sensor2.pin_1, sensor3.pin_1, sensor4.pin_1, 1up.3, 4do.1, 4do.2, 24c32.A1
  VCC: CJMCU2317.VCC, WeMos_D1_Mini1.3V3, part_2.Pin_1, 24c32.+V
  N3: CJMCU2317.RESET, WeMos_D1_Mini1.D4
  N4: CJMCU2317.GPB0, 1up.2
  N5: CJMCU2317.GPB1, 1do.2
  N6: CJMCU2317.GPB2, 2up.2
  N7: CJMCU2317.GPB3, 2do.2
  N8: CJMCU2317.GPB4, 3up.4
  N9: CJMCU2317.GPB5, 3do.4
  N10: CJMCU2317.GPB6, 4up.4
  N11: CJMCU2317.GPB7, 4do.4
  N12: CJMCU2317.GPA0, 8_Channel_Relay_active_high.IN1
  N13: CJMCU2317.GPA1, 8_Channel_Relay_active_high.IN2
  N14: CJMCU2317.GPA2, 8_Channel_Relay_active_high.IN3
  N15: CJMCU2317.GPA3, 8_Channel_Relay_active_high.IN4
  N16: CJMCU2317.GPA4, 8_Channel_Relay_active_high.IN5
  N17: CJMCU2317.GPA5, 8_Channel_Relay_active_high.IN6
  N18: CJMCU2317.GPA6, 8_Channel_Relay_active_high.IN7
  N19: CJMCU2317.GPA7, 8_Channel_Relay_active_high.IN8
  VCC_2: 8_Channel_Relay_active_high.VCC, WeMos_D1_Mini1.5V
  N20: 8_Channel_Relay_active_high.COM#22, 8_Channel_Relay_active_high.NC
  N21: 8_Channel_Relay_active_high.NO#23, motor.pin1, motor.pin_4
  N22: 8_Channel_Relay_active_high.COM#25, 220v_in.pin3, 220v_in.pin_6
  N23: 8_Channel_Relay_active_high.NO#26, motor.pin3, motor.pin_6
  N24: WeMos_D1_Mini1.A0, part_2.Pin_0
  N25: WeMos_D1_Mini1.D0, part.Pin_1
  N26: WeMos_D1_Mini1.D5, sensor2.pin_2
  N27: WeMos_D1_Mini1.D6, sensor3.pin_2
  N28: WeMos_D1_Mini1.D7, sensor4.pin_2
  N29: WeMos_D1_Mini1.RX, sensor1.pin_2
  N30: motor.pin_5, 220v_in.pin2, 220v_in.pin_5
  N31: 24c32.A0, 24c32.A2
  N32: 24c32.0V, 24c32.WP_-_Write_Protect

custom parts:
  CJMCU2317-MCP23017: The MCP23017 device family provides 16-bit, general purpose parallel I/O expansion for I2C bus. The MCP23X17 consists of multiple 8-bit configuration registers for input, output and polarity selection. The system master can enable the I/Os as either inputs or outputs by writing the I/O configuration bits (IODIRA/B). The data for each input or output is kept in the corresponding input or output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
  8 Channel Power Relay: An 8 channel power relay. The module operates at 5V.
