# Fritzing sketch ESP RGBW LED (saved by Fritzing 0.9.3b)
circuit board: 8.46667cm x 5.64444cm

parts:
  Q3-G = Basic FET N-Channel [package="DPak [SMD]"]
  R3 = Resistor [tolerance=±5% resistance=6.8k package="0402 [SMD]"]
  Q2-R = Basic FET N-Channel [package="DPak [SMD]"]
  R2 = Resistor [tolerance=±5% resistance=6.8k package="0402 [SMD]"]
  Q1-B = Basic FET N-Channel [package="DPak [SMD]"]
  R1 = Resistor [tolerance=±5% resistance=6.8k package="0402 [SMD]"]
  WeMos_D1_Mini1 = WeMos D1 Mini
  Q3-G1 = Basic FET N-Channel [package="DPak [SMD]"]
  R4 = Resistor [tolerance=±5% resistance=6.8k package="0402 [SMD]"]
  R5 = Resistor [tolerance=±5% resistance=220 package=THT]
  R6 = Resistor [tolerance=±5% resistance=220 package=THT]
  R7 = Resistor [tolerance=±5% resistance=220 package=THT]
  R8 = Resistor [tolerance=±5% resistance=220 package=THT]
  on/off = Pushbutton [package="[THT]"]
  Dc_12V = Power plug
  7805 = Voltage Regulator [package=78xxl]
  part = Electrolytic Capacitor [capacitance=10µF package="100 mil [THT, electrolytic]"]
  B_G_R_W_+ = Camdenboss CTB0158-5 [part_number=CTB0158-5 package=THT]

nets:
  N1: Q3-G.Gate, R3.Pin_1
  N2: Q3-G.drain, B_G_R_W_+.pin3
  N3: Q3-G.source, R3.Pin_0, Q3-G1.source, R4.Pin_0
  N4: Q2-R.Gate, R2.Pin_1, R6.Pin_1
  N5: Q2-R.drain, B_G_R_W_+.pin2
  N6: Q2-R.source, R2.Pin_0
  N7: Q1-B.Gate, R1.Pin_1
  N8: Q1-B.drain, B_G_R_W_+.pin1
  N9: Q1-B.source, R1.Pin_0
  N10: WeMos_D1_Mini1.5V, 7805.OUT, part.-
  N11: WeMos_D1_Mini1.D1, R8.Pin_0
  N12: WeMos_D1_Mini1.D3, on/off.Pin_1, on/off.Pin_2
  N13: WeMos_D1_Mini1.D5, R7.Pin_0
  N14: WeMos_D1_Mini1.D6, R6.Pin_0
  N15: WeMos_D1_Mini1.D7, R5.Pin_0
  N16: WeMos_D1_Mini1.G, on/off.Pin_3, on/off.Pin_4, 7805.GND
  N17: Q3-G1.Gate, R4.Pin_1
  N18: Q3-G1.drain, B_G_R_W_+.pin4
  N19: Dc_12V.VCC, 7805.IN, B_G_R_W_+.pin5
