# Fritzing sketch lcd_i2c (1) (saved by Fritzing 0.9.3b)

parts:
  U4 = LCD-16X2 [package=lcd-16x2_noholes]
  WeMos_D1_Mini1 = WeMos D1 Mini
  S1 = Momentary Switch [package=ksa_sealed_tac_switch]
  S2 = Momentary Switch [package=ksa_sealed_tac_switch]
  S3 = Momentary Switch [package=ksa_sealed_tac_switch]
  S4 = Momentary Switch [package=ksa_sealed_tac_switch]
  S5 = Momentary Switch [package=ksa_sealed_tac_switch]
  S6 = Momentary Switch [package=ksa_sealed_tac_switch]
  R1 = Resistor [tolerance=±5% resistance=4.7k package="2512 [SMD]"]
  R2 = Resistor [tolerance=±5% resistance=4.7k package="2512 [SMD]"]
  R3 = Resistor [tolerance=±5% resistance=4.7k package="2512 [SMD]"]
  R4 = Resistor [tolerance=±5% resistance=4.7k package="2512 [SMD]"]  # not connected
  R5 = Resistor [tolerance=±5% resistance=4.7k package="2512 [SMD]"]  # not connected
  R6 = Resistor [tolerance=±5% resistance=4.7k package="2512 [SMD]"]

nets:
  N1: U4.VSS, S5.2, S6.1
  VDD: U4.VDD, WeMos_D1_Mini1.5V
  N2: U4.A, WeMos_D1_Mini1.D2
  N3: U4.K, WeMos_D1_Mini1.D1
  N4: WeMos_D1_Mini1.3V3, R1.Pin_0
  N5: WeMos_D1_Mini1.D0, S1.2
  N6: WeMos_D1_Mini1.D3, S2.3
  N7: WeMos_D1_Mini1.D4, S3.3
  N8: WeMos_D1_Mini1.D5, S4.3
  N9: WeMos_D1_Mini1.D6, S5.3
  N10: WeMos_D1_Mini1.D7, S6.3
  N11: WeMos_D1_Mini1.G, S1.4
  N12: S1.1, R1.Pin_1
  N13: S1.3, S2.1
  N14: S2.2, S3.1
  N15: S2.4, R2.Pin_1
  N16: S3.2, S4.1
  N17: S3.4, R3.Pin_1
  N18: S4.2, S5.1
  N19: S6.4, R6.Pin_1
