# Fritzing sketch mcp23017 16 X 16 (saved by Fritzing 0.9.3b)

parts:
  WeMos_D1_Mini1 = WeMos D1 Mini
  MCP23017 = CJMCU2317-MCP23017
  High_level_triger_relay = 4-Channel 5v Relay Shield [package=relay-4ch5v10a]
  High_level_triger_relay_2 = 4-Channel 5v Relay Shield [package=relay-4ch5v10a]
  High_level_triger_relay_3 = 4-Channel 5v Relay Shield [package=relay-4ch5v10a]
  WiFiConfig = Pushbutton [package="[THT]"]
  High_level_triger_relay1 = 4-Channel 5v Relay Shield [package=relay-4ch5v10a]
  MCP23017_2 = CJMCU2317-MCP23017
  S1 = Pushbutton [package="[THT]"]
  S2 = Pushbutton [package="[THT]"]
  S3 = Pushbutton [package="[THT]"]
  S4 = Pushbutton [package="[THT]"]
  S5 = Pushbutton [package="[THT]"]
  S6 = Pushbutton [package="[THT]"]
  S7 = Pushbutton [package="[THT]"]
  S8 = Pushbutton [package="[THT]"]
  S9 = Pushbutton [package="[THT]"]
  S10 = Pushbutton [package="[THT]"]
  S11 = Pushbutton [package="[THT]"]
  S12 = Pushbutton [package="[THT]"]
  S13 = Pushbutton [package="[THT]"]
  P_1 = Pushbutton [package="[THT]"]
  P_16 = Pushbutton [package="[THT]"]
  S16 = Pushbutton [package="[THT]"]

nets:
  VCC: WeMos_D1_Mini1.3V3, MCP23017.VCC, MCP23017_2.VCC
  5V: WeMos_D1_Mini1.5V, High_level_triger_relay_3.VCC
  N1: WeMos_D1_Mini1.D1, MCP23017.SCL/SCLK, MCP23017_2.SCL/SCLK
  N2: WeMos_D1_Mini1.D2, MCP23017.SDA/SDI/SDO, MCP23017_2.SDA/SDI/SDO
  N3: WeMos_D1_Mini1.D3, WiFiConfig.Pin_1
  N4: WeMos_D1_Mini1.D4, MCP23017.RESET, MCP23017_2.RESET
  GND: WeMos_D1_Mini1.G, MCP23017.GND, WiFiConfig.Pin_3, WiFiConfig.Pin_4, MCP23017_2.GND
  N5: MCP23017.GPB0, High_level_triger_relay_3.IN1
  N6: MCP23017.GPB1, High_level_triger_relay_3.IN2
  N7: MCP23017.GPB2, High_level_triger_relay_3.IN3
  N8: MCP23017.GPB3, High_level_triger_relay_3.IN4
  N9: MCP23017.GPB4, High_level_triger_relay1.IN1
  N10: MCP23017.GPB5, High_level_triger_relay1.IN2
  N11: MCP23017.GPB6, High_level_triger_relay1.IN3
  N12: MCP23017.GPB7, High_level_triger_relay1.IN4
  N13: MCP23017.GPA0, High_level_triger_relay.IN1
  N14: MCP23017.GPA1, High_level_triger_relay.IN2
  N15: MCP23017.GPA2, High_level_triger_relay.IN3
  N16: MCP23017.GPA3, High_level_triger_relay.IN4
  N17: MCP23017.GPA4, High_level_triger_relay_2.IN1
  N18: MCP23017.GPA5, High_level_triger_relay_2.IN2
  N19: MCP23017.GPA6, High_level_triger_relay_2.IN3
  N20: MCP23017.GPA7, High_level_triger_relay_2.IN4
  VCC_2: High_level_triger_relay.VCC, High_level_triger_relay_2.VCC, High_level_triger_relay1.VCC
  N21: MCP23017_2.GPB0, S6.Pin_3, S6.Pin_4
  N22: MCP23017_2.GPB1, S5.Pin_1, S5.Pin_2
  N23: MCP23017_2.GPB2, S4.Pin_1, S4.Pin_2
  N24: MCP23017_2.GPB3, S3.Pin_3, S3.Pin_4
  N25: MCP23017_2.GPB4, S2.Pin_3, S2.Pin_4
  N26: MCP23017_2.GPB5, S1.Pin_3, S1.Pin_4
  N27: MCP23017_2.GPB6, S16.Pin_3, S16.Pin_4
  N28: MCP23017_2.GPB7, P_16.Pin_1, P_16.Pin_2
  N29: MCP23017_2.GPA0, P_1.Pin_3, P_1.Pin_4
  N30: MCP23017_2.GPA1, S13.Pin_1, S13.Pin_2
  N31: MCP23017_2.GPA2, S12.Pin_1, S12.Pin_2
  N32: MCP23017_2.GPA3, S11.Pin_1, S11.Pin_2
  N33: MCP23017_2.GPA4, S10.Pin_1, S10.Pin_2
  N34: MCP23017_2.GPA5, S9.Pin_1, S9.Pin_2
  N35: MCP23017_2.GPA6, S8.Pin_1, S8.Pin_2
  N36: MCP23017_2.GPA7, S7.Pin_3, S7.Pin_4

custom parts:
  CJMCU2317-MCP23017: The MCP23017 device family provides 16-bit, general purpose parallel I/O expansion for I2C bus. The MCP23X17 consists of multiple 8-bit configuration registers for input, output and polarity selection. The system master can enable the I/Os as either inputs or outputs by writing the I/O configuration bits (IODIRA/B). The data for each input or output is kept in the corresponding input or output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
  4-Channel 5v Relay Shield: 4 Channel 5v Relay Shield w. 2x SPD-06VDC-SD-C
