# Fritzing sketch 3_x_Telegram (saved by Fritzing 0.9.3b)

parts:
  WeMos_D1_Mini1 = WeMos D1 Mini
  Wifi_config = Pushbutton [package="[THT]"]
  in1_in2_in3_G = Camdenboss CTB0158-4 [part_number=CTB0158-4 package=THT]

nets:
  N1: WeMos_D1_Mini1.D3, Wifi_config.Pin_1, Wifi_config.Pin_2
  N2: WeMos_D1_Mini1.D5, in1_in2_in3_G.pin4
  N3: WeMos_D1_Mini1.D6, in1_in2_in3_G.pin3
  N4: WeMos_D1_Mini1.D7, in1_in2_in3_G.pin2
  N5: WeMos_D1_Mini1.G, Wifi_config.Pin_3, Wifi_config.Pin_4, in1_in2_in3_G.pin1
