# Fritzing sketch ir (saved by Fritzing 0.9.3b)

parts:
  IR1 = TSOP312.., 314.. [package=THT]
  R1 = Resistor [tolerance=±5% resistance=100 package=THT]
  C1 = Electrolytic Capacitor [capacitance=10µF package="100 mil [THT, electrolytic]"]

nets:
  GND: IR1.GND, C1.-
  N1: IR1.Vs, R1.Pin_1, C1.+
  RX: IR1.Data
  + 3.3: R1.Pin_0
