# Fritzing sketch Supla_12x12_2NO_DS_Ms (saved by Fritzing 0.9.3b)

parts:
  MPR121 = MPR121 Breakout
  WeMos_D1_Mini1 = WeMos D1 Mini
  MCP23017 = CJMCU2317-MCP23017
  High_level_triger_relay = 4-Channel 5v Relay Shield [package=relay-4ch5v10a]
  High_level_triger_relay_2 = 4-Channel 5v Relay Shield [package=relay-4ch5v10a]
  High_level_triger_relay_3 = 4-Channel 5v Relay Shield [package=relay-4ch5v10a]
  U11 = TOUCH [package=touch2]
  U12 = TOUCH [package=touch2]
  U13 = TOUCH [package=touch2]
  U14 = TOUCH [package=touch2]
  U15 = TOUCH [package=touch2]
  U16 = TOUCH [package=touch2]
  U17 = TOUCH [package=touch2]
  U18 = TOUCH [package=touch2]
  U19 = TOUCH [package=touch2]
  touch = TOUCH [package=touch2]
  U21 = TOUCH [package=touch2]
  U22 = TOUCH [package=touch2]
  Rain_Sensor = Reed switch [package=THT]
  Sensor_2 = Reed switch [package=THT]
  part = DS18B20 1-Wire Temperature Sensor [part_number=DS18B20]

nets:
  N1: MPR121.SCL, WeMos_D1_Mini1.D1, MCP23017.SCL/SCLK
  N2: MPR121.SDA, WeMos_D1_Mini1.D2, MCP23017.SDA/SDI/SDO
  N3: MPR121.ELE11, touch.T2
  N4: MPR121.ELE10, U16.T2
  N5: MPR121.ELE9, U19.T1, U19.T2
  N6: MPR121.ELE8, U14.T2
  N7: MPR121.ELE7, U15.T1, U15.T2
  N8: MPR121.ELE6, U11.T1, U11.T2
  N9: MPR121.ELE5, U13.T2
  N10: MPR121.ELE4, U12.T1, U12.T2
  N11: MPR121.ELE3, U18.T1, U18.T2
  N12: MPR121.ELE2, U17.T2
  N13: MPR121.ELE1, U22.T1, U22.T2
  N14: MPR121.ELE0, U21.T2
  3.3V: MPR121.3.3V, WeMos_D1_Mini1.3V3, MCP23017.VCC, part.VDD
  GND: MPR121.GND, WeMos_D1_Mini1.G, MCP23017.GND, part.GND
  N15: WeMos_D1_Mini1.D4, MCP23017.RESET
  N16: WeMos_D1_Mini1.D5, Rain_Sensor.pin_1
  N17: WeMos_D1_Mini1.D6, Sensor_2.pin_1
  N18: WeMos_D1_Mini1.D7, part.DQ
  N19: MCP23017.ADDR2, MCP23017.ADDR1, MCP23017.ADDR0
  N20: MCP23017.GPB0, High_level_triger_relay_3.IN1
  N21: MCP23017.GPB1, High_level_triger_relay_3.IN2
  N22: MCP23017.GPB2, High_level_triger_relay_3.IN3
  N23: MCP23017.GPB3, High_level_triger_relay_3.IN4
  N24: MCP23017.GPA0, High_level_triger_relay.IN1
  N25: MCP23017.GPA1, High_level_triger_relay.IN2
  N26: MCP23017.GPA2, High_level_triger_relay.IN3
  N27: MCP23017.GPA3, High_level_triger_relay.IN4
  N28: MCP23017.GPA4, High_level_triger_relay_2.IN1
  N29: MCP23017.GPA5, High_level_triger_relay_2.IN2
  N30: MCP23017.GPA6, High_level_triger_relay_2.IN3
  N31: MCP23017.GPA7, High_level_triger_relay_2.IN4
  VCC: High_level_triger_relay.VCC, High_level_triger_relay_2.VCC

custom parts:
  CJMCU2317-MCP23017: The MCP23017 device family provides 16-bit, general purpose parallel I/O expansion for I2C bus. The MCP23X17 consists of multiple 8-bit configuration registers for input, output and polarity selection. The system master can enable the I/Os as either inputs or outputs by writing the I/O configuration bits (IODIRA/B). The data for each input or output is kept in the corresponding input or output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
  4-Channel 5v Relay Shield: 4 Channel 5v Relay Shield w. 2x SPD-06VDC-SD-C
