# Fritzing sketch aux_board (saved by Fritzing 0.9.3b)
breadboards: 1

parts:
  IR1 = TSOP312.., 314.. [package=THT]
  R2 = Resistor [tolerance=±5% resistance=100 part_number="27Ω - 120Ω" package=THT]
  C1 = Electrolytic Capacitor [capacitance=10µF part_number="4.7µF - 47µF" package="100 mil [THT, electrolytic]"]
  WiFiConfig = Pushbutton [part_number=WiFiConfig package=THT]
  AT_0 = Pushbutton [package=THT]
  AT_1 = Pushbutton [package=THT]

nets:
  GND: IR1.GND, C1.-, WiFiConfig.leg1, AT_0.leg1, AT_1.leg1
  N1: IR1.Vs, C1.+
  Gpio 14: IR1.Data
  +3.3v: R2.Pin_1
  Gpio 0: WiFiConfig.leg0
  Gpio 5: AT_0.leg0
  Gpio4: AT_1.leg0
