# Fritzing sketch supla_595_2 (saved by Fritzing 0.9.3b)

parts:
  WeMos_D1_Mini1 = WeMos D1 Mini
  U1 = 74HC595 [package="DIP16 [THT]"]
  S1 = Pushbutton [package="[THT]"]
  R2 = Resistor [tolerance=±5% resistance=4.7k package=THT]
  U2 = 4-Channel 5v Relay Shield [package=relay-4ch5v10a]
  U3 = 4-Channel 5v Relay Shield [package=relay-4ch5v10a]
  S2 = Pushbutton [package="[THT]"]
  R3 = Resistor [tolerance=±5% resistance=4.7k package=THT]
  S3 = Pushbutton [package="[THT]"]
  R4 = Resistor [tolerance=±5% resistance=4.7k package=THT]
  S4 = Pushbutton [package="[THT]"]
  R5 = Resistor [tolerance=±5% resistance=4.7k package=THT]
  S5 = Pushbutton [package="[THT]"]
  R6 = Resistor [tolerance=±5% resistance=4.7k package=THT]
  S6 = Pushbutton [package="[THT]"]
  R7 = Resistor [tolerance=±5% resistance=4.7k package=THT]
  S7 = Pushbutton [package="[THT]"]
  R8 = Resistor [tolerance=±5% resistance=4.7k package=THT]
  S8 = Pushbutton [package="[THT]"]
  R9 = Resistor [tolerance=±5% resistance=4.7k package=THT]

nets:
  3V3: WeMos_D1_Mini1.3V3, U1.MR, U1.VCC, R4.Pin_1
  VCC: WeMos_D1_Mini1.5V, U2.VCC, U3.VCC
  N1: WeMos_D1_Mini1.D0, U1.SH_CP
  N2: WeMos_D1_Mini1.D1, S7.Pin_1, S7.Pin_2, R8.Pin_0
  N3: WeMos_D1_Mini1.D2, S6.Pin_1, S6.Pin_2, R7.Pin_0
  N4: WeMos_D1_Mini1.D3, U1.ST_CP
  N5: WeMos_D1_Mini1.D4, S5.Pin_1, S5.Pin_2, R6.Pin_0
  N6: WeMos_D1_Mini1.D5, S4.Pin_1, S4.Pin_2, R5.Pin_0
  N7: WeMos_D1_Mini1.D6, S3.Pin_1, S3.Pin_2, R4.Pin_0
  N8: WeMos_D1_Mini1.D7, S2.Pin_1, S2.Pin_2, R3.Pin_0
  N9: WeMos_D1_Mini1.D8, U1.DS
  GND: WeMos_D1_Mini1.G, U1.GND, U1.OE, S1.Pin_3, S1.Pin_4, U2.GND, U3.GND, S2.Pin_3, S2.Pin_4, S3.Pin_3, S3.Pin_4, S4.Pin_3, S4.Pin_4, S5.Pin_3, S5.Pin_4, S6.Pin_3, S6.Pin_4, S7.Pin_3, S7.Pin_4, S8.Pin_3, S8.Pin_4
  N10: WeMos_D1_Mini1.RX, WeMos_D1_Mini1.TX, S1.Pin_1, S1.Pin_2, R2.Pin_0, S8.Pin_1, S8.Pin_2, R9.Pin_0
  N11: U1.Q1, U2.IN3
  N12: U1.Q2, U2.IN2
  N13: U1.Q3, U2.IN1
  N14: U1.Q4, U3.IN4
  N15: U1.Q5, U3.IN3
  N16: U1.Q6, U3.IN2
  N17: U1.Q7, U3.IN1
  N18: U1.Q0, U2.IN4

notes:
  D1-D2-D4-D5-D6-D7-RX-TX
  btn --- imput

custom parts:
  4-Channel 5v Relay Shield: 4 Channel 5v Relay Shield w. 2x SPD-06VDC-SD-C
