# Fritzing sketch supla_595_8x8_Ntc (saved by Fritzing 0.9.3b)
circuit board: 8.46667cm x 5.64444cm
breadboards: 1

parts:
  WeMos_D1_Mini1 = WeMos D1 Mini
  U1 = 74HC595 [part_number=1-8 package="DIP16 [THT]"]
  LED1 = smd LED [color="Red (633nm)" package="1206 [SMD]"]
  LED2 = smd LED [color="Red (633nm)" package="1206 [SMD]"]
  LED3 = smd LED [color="Red (633nm)" package="1206 [SMD]"]
  LED4 = smd LED [color="Red (633nm)" package="1206 [SMD]"]
  LED5 = smd LED [color="Red (633nm)" package="1206 [SMD]"]
  LED6 = smd LED [color="Red (633nm)" package="1206 [SMD]"]
  LED7 = smd LED [color="Red (633nm)" package="1206 [SMD]"]
  LED8 = smd LED [color="Red (633nm)" package="1206 [SMD]"]
  R9 = Resistor [tolerance=±5% resistance=220 package=THT]
  R2 = Resistor [tolerance=±5% resistance=220 package=THT]
  R3 = Resistor [tolerance=±5% resistance=220 package=THT]
  R4 = Resistor [tolerance=±5% resistance=220 package=THT]
  R5 = Resistor [tolerance=±5% resistance=220 package=THT]
  R6 = Resistor [tolerance=±5% resistance=220 package=THT]
  R7 = Resistor [tolerance=±5% resistance=220 package=THT]
  R8 = Resistor [tolerance=±5% resistance=220 package=THT]
  R10 = Temperature Sensor (Thermistor) [thermistor_type=NTC package=THT]
  R11 = Resistor [tolerance=±5% resistance=100k package="0603 [SMD]"]

nets:
  3V3: WeMos_D1_Mini1.3V3, U1.MR, U1.VCC, R11.Pin_0
  N1: WeMos_D1_Mini1.A0, R10.pin_0, R11.Pin_1
  N2: WeMos_D1_Mini1.D0, U1.SH_CP
  N3: WeMos_D1_Mini1.D3, U1.ST_CP
  N4: WeMos_D1_Mini1.D8, U1.DS
  N5: WeMos_D1_Mini1.G, U1.GND, U1.OE, R9.Pin_0, R2.Pin_0, R3.Pin_0, R4.Pin_0, R5.Pin_0, R6.Pin_0, R7.Pin_0, R8.Pin_0, R10.pin_1
  N6: U1.Q1, LED1.anode
  N7: U1.Q2, LED2.anode
  N8: U1.Q3, LED3.anode
  N9: U1.Q4, LED4.anode
  N10: U1.Q5, LED5.anode
  N11: U1.Q6, LED6.anode
  N12: U1.Q7, LED7.anode
  N13: U1.Q0, LED8.anode
  N14: LED1.cathode, R2.Pin_1
  N15: LED2.cathode, R3.Pin_1
  N16: LED3.cathode, R4.Pin_1
  N17: LED4.cathode, R5.Pin_1
  N18: LED5.cathode, R6.Pin_1
  N19: LED6.cathode, R7.Pin_1
  N20: LED7.cathode, R8.Pin_1
  N21: LED8.cathode, R9.Pin_1

notes:
  D1-D2-D4-D5-D6-D7-RX-TX
  btn --- imput 1 to 8
  10kΩ NTC
