# Fritzing sketch mpx_3.3 (saved by Fritzing 0.9.3b)

parts:
  MPX1 = MPX2010 pressure sensor [part_number=MPX]
  Wifi_Configuration = Momentary Switch [package=ksa_sealed_tac_switch]
  zero = Momentary Switch [package=ksa_sealed_tac_switch]
  R1 = Resistor [tolerance=±5% resistance=150k package=THT]
  WeMos_D1_Mini1 = WeMos D1 Mini

nets:
  N1: MPX1.GND, R1.Pin_0
  N2: MPX1.V_out_-, zero.2
  N3: MPX1.Vs, WeMos_D1_Mini1.5V
  N4: Wifi_Configuration.1, zero.1
  N5: Wifi_Configuration.2, WeMos_D1_Mini1.G
  N6: Wifi_Configuration.4, WeMos_D1_Mini1.D3
  N7: zero.3, WeMos_D1_Mini1.D5
  N8: R1.Pin_1, WeMos_D1_Mini1.A0
