# Fritzing sketch 12Bar (saved by Fritzing 0.9.3b)

parts:
  zero = Momentary Switch [package=ksa_sealed_tac_switch]
  part = Resistor [tolerance=±5% resistance=180k package=THT]
  5v_Gnd_An = Camdenboss CTB0158-3 [part_number=CTB0158-3 package=THT]
  U1 = NodeMCU V3.0

nets:
  N1: zero.1, 5v_Gnd_An.pin2, U1.GND
  N2: zero.3, U1.D5
  N3: part.Pin_0, 5v_Gnd_An.pin3
  N4: part.Pin_1, U1.A0
  N5: 5v_Gnd_An.pin1, U1.Vin

custom parts:
  NodeMCU V3.0: ESP8266 based NodeMCU
