# Fritzing sketch 12BarV2 (saved by Fritzing 0.9.3b)

parts:
  zero = Momentary Switch [package=ksa_sealed_tac_switch]
  part = Resistor [tolerance=±5% resistance=180k package=THT]
  5v_Gnd_An = Camdenboss CTB0158-3 [part_number=CTB0158-3 package=THT]
  U1 = NodeMCU V3.0
  Active_HIGH = 4-Channel 5v Relay Shield [package=relay-4ch5v10a]
  S1 = Reed switch [package=THT]
  S2 = Reed switch [package=THT]
  part_2 = DS18B20 1-Wire Temperature Sensor [part_number=DS18B20]
  part_3 = DS18B20 1-Wire Temperature Sensor [part_number=DS18B20]
  R1 = Resistor [tolerance=±5% resistance=4.7k package=THT]

nets:
  GND: zero.1, 5v_Gnd_An.pin2, U1.GND, S1.pin_1, S2.pin_1, part_2.GND, part_3.GND
  N1: zero.2, Active_HIGH.GND
  N2: zero.3, U1.D5
  N3: part.Pin_0, 5v_Gnd_An.pin3
  N4: part.Pin_1, U1.A0
  VIN: 5v_Gnd_An.pin1, U1.Vin, Active_HIGH.VCC
  N5: U1.D1, S1.pin_2
  N6: U1.D2, S2.pin_2
  VDD: U1.3V3, part_2.VDD, part_3.VDD, R1.Pin_1
  N7: U1.D6, Active_HIGH.IN1
  N8: U1.D7, Active_HIGH.IN2
  N9: U1.D8, Active_HIGH.IN3
  N10: U1.RX, part_2.DQ, part_3.DQ, R1.Pin_0

custom parts:
  NodeMCU V3.0: ESP8266 based NodeMCU
  4-Channel 5v Relay Shield: 4 Channel 5v Relay Shield w. 2x SPD-06VDC-SD-C
