# Fritzing sketch 12BarV2 (saved by Fritzing 0.9.3b)

parts:
  manual = Momentary Switch [package=ksa_sealed_tac_switch]
  part = Resistor [tolerance=±5% resistance=180k package=THT]
  5v_Gnd_An = Camdenboss CTB0158-3 [part_number=CTB0158-3 package=THT]
  U1 = NodeMCU V3.0
  S1 = Reed switch [package=THT]
  S2 = Reed switch [package=THT]
  part_2 = DS18B20 1-Wire Temperature Sensor [part_number=DS18B20]
  part_3 = DS18B20 1-Wire Temperature Sensor [part_number=DS18B20]
  R1 = Resistor [tolerance=±5% resistance=4.7k package=THT]
  o1 = Module display OLED I2C 128x64 SSD1306 [package=THT]
  config = Pushbutton [package="[THT]"]
  U2 = 2-Channel 5v Relay Shield [package=relay-2ch5v10a]

nets:
  GND: manual.1, 5v_Gnd_An.pin2, U1.GND#6, U1.GND#13, U1.GND#33, S1.pin_1, S2.pin_1, part_2.GND, part_3.GND
  N1: manual.2, config.Pin_3, config.Pin_4, U2.GND
  N2: manual.3, U1.D5
  N3: part.Pin_0, 5v_Gnd_An.pin3
  N4: part.Pin_1, U1.A0
  VIN: 5v_Gnd_An.pin1, U1.Vin, U2.VCC
  N5: U1.D1, S1.pin_2
  N6: U1.D2, S2.pin_2
  N7: U1.D3, o1.SDA
  N8: U1.D4, o1.SCL
  VDD: U1.3V3, part_2.VDD, part_3.VDD, R1.Pin_1, o1.VCC
  N9: U1.D6, config.Pin_1
  N10: U1.D7, U2.IN1
  N11: U1.D8, U2.IN2
  N12: U1.RX, part_2.DQ, part_3.DQ, R1.Pin_0
  N13: U1.GND#41, o1.GND

custom parts:
  NodeMCU V3.0: ESP8266 based NodeMCU
  Module display OLED I2C 128x64 SSD1306: Ecran OLED I2C SSD163 de 128x64 avec connexion I2C
  2-Channel 5v Relay Shield: 2 Channel 5v Relay Shield w. 2x SPD-06VDC-SD-C
