# Fritzing sketch suplaS7 (saved by Fritzing 0.9.3b)

parts:
  U1 = 74HC4051 [package=so16]
  WeMos_D1_Mini1 = WeMos D1 Mini
  R1 = Resistor [tolerance=±5% resistance=180k package=THT]
  R2 = Resistor [tolerance=±5% resistance=1M package=THT]
  R3 = Resistor [tolerance=±5% resistance=330k package=THT]
  R6 = Resistor [tolerance=±5% resistance=1M package=THT]
  R7 = Resistor [tolerance=±5% resistance=330k package=THT]
  R8 = Resistor [tolerance=±5% resistance=1M package=THT]
  R9 = Resistor [tolerance=±5% resistance=330k package=THT]
  part = Resistor [tolerance=±5% resistance=1M package=THT]
  part_2 = Resistor [tolerance=±5% resistance=330k package=THT]
  R12 = Resistor [tolerance=±5% resistance=1M package=THT]
  R13 = Resistor [tolerance=±5% resistance=330k package=THT]
  R14 = Resistor [tolerance=±5% resistance=1M package=THT]
  R15 = Resistor [tolerance=±5% resistance=330k package=THT]
  R16 = Resistor [tolerance=±5% resistance=1M package=THT]
  R17 = Resistor [tolerance=±5% resistance=330k package=THT]

nets:
  N1: U1.IO4, R8.Pin_1, R9.Pin_0
  N2: U1.IO6, R6.Pin_1, R7.Pin_0
  N3: U1.IO, R1.Pin_0
  N4: U1.IO5, R2.Pin_1, R3.Pin_0
  N5: U1.INH, U1.VEE, U1.VSS, WeMos_D1_Mini1.G, R3.Pin_1
  N6: U1.C, WeMos_D1_Mini1.D7
  N7: U1.B, WeMos_D1_Mini1.D6
  N8: U1.A, WeMos_D1_Mini1.D5
  N9: U1.IO3, part.Pin_1, part_2.Pin_0
  N10: U1.IO0, R12.Pin_1, R13.Pin_0
  N11: U1.IO1, R14.Pin_1, R15.Pin_0
  N12: U1.IO2, R16.Pin_1, R17.Pin_0
  VDD: U1.VDD, WeMos_D1_Mini1.5V
  N13: WeMos_D1_Mini1.A0, R1.Pin_1

notes:
  An3
  An2
  An1
  An4
  An5
  An7
  An6
