# Fritzing sketch termostat (saved by Fritzing 0.9.3b)

parts:
  U1 = 2-Channel 5v Relay Shield [package=relay-2ch5v10a]
  WeMos_D1_Mini1 = WeMos D1 Mini
  part = DS18B20 1-Wire Temperature Sensor [part_number=DS18B20]
  Auto/Man = LED - 5mm [color="Red (633nm)" package="5 mm [THT]"]
  status_led = LED - 5mm [color="Green (560nm)" package="5 mm [THT]"]
  Manual_on/off = Pushbutton [package="[THT]"]
  termostat_Auto/Man_+_wificonfig = Pushbutton [package="[THT]"]

nets:
  VCC: U1.VCC, WeMos_D1_Mini1.5V
  N1: U1.IN1, WeMos_D1_Mini1.D7
  3V3: WeMos_D1_Mini1.3V3, part.VDD, status_led.anode
  N2: WeMos_D1_Mini1.A0, status_led.cathode
  N3: WeMos_D1_Mini1.D1, Manual_on/off.Pin_3, Manual_on/off.Pin_4
  N4: WeMos_D1_Mini1.D2, termostat_Auto/Man_+_wificonfig.Pin_3, termostat_Auto/Man_+_wificonfig.Pin_4
  N5: WeMos_D1_Mini1.D4, part.DQ
  N6: WeMos_D1_Mini1.D6, Auto/Man.anode
  N7: WeMos_D1_Mini1.G, part.GND, Auto/Man.cathode, Manual_on/off.Pin_1, Manual_on/off.Pin_2, termostat_Auto/Man_+_wificonfig.Pin_1, termostat_Auto/Man_+_wificonfig.Pin_2

custom parts:
  2-Channel 5v Relay Shield: 2 Channel 5v Relay Shield w. 2x SPD-06VDC-SD-C
