# Fritzing sketch thermostat_oled (saved by Fritzing 0.9.3b)

parts:
  DS1 = DS18B20 1-Wire Temperature Sensor [part_number=DS18B20]
  WeMos_D1_Mini1 = WeMos D1 Mini
  SSD1306 = Module display OLED I2C 128x64 SSD1306 [package=THT]
  Relay = RELAY-SOLIDSTATE [package=relay-s108t02]
  aut_/_man = Pushbutton [package="[THT]"]
  on/off = Pushbutton [package="[THT]"]
  -0_5º = Pushbutton [package="[THT]"]
  +0_5º = Pushbutton [package="[THT]"]
  R1 = Resistor [tolerance=±5% resistance=4.7k package=THT]  # not connected
  R2 = Resistor [tolerance=±5% resistance=10k package=THT]
  R3 = Resistor [tolerance=±5% resistance=220 package=THT]
  thermometer_Auto/Man_Led = LED - 5mm [color="Red (633nm)" package="5 mm [THT]"]

nets:
  N1: DS1.DQ, WeMos_D1_Mini1.D7
  VDD: DS1.VDD, WeMos_D1_Mini1.3V3, SSD1306.VCC, R2.Pin_1
  N2: WeMos_D1_Mini1.D0, on/off.Pin_4, R2.Pin_0
  N3: WeMos_D1_Mini1.D1, -0_5º.Pin_1, -0_5º.Pin_2
  N4: WeMos_D1_Mini1.D2, +0_5º.Pin_1, +0_5º.Pin_2
  N5: WeMos_D1_Mini1.D3, SSD1306.SDA
  N6: WeMos_D1_Mini1.D4, SSD1306.SCL
  N7: WeMos_D1_Mini1.D5, aut_/_man.Pin_2
  N8: WeMos_D1_Mini1.D6, Relay.+
  N9: WeMos_D1_Mini1.D8, R3.Pin_1
  N10: Relay.-, aut_/_man.Pin_3, aut_/_man.Pin_4, on/off.Pin_1, on/off.Pin_2, -0_5º.Pin_3, -0_5º.Pin_4, +0_5º.Pin_3
  N11: R3.Pin_0, thermometer_Auto/Man_Led.cathode

custom parts:
  Module display OLED I2C 128x64 SSD1306: Ecran OLED I2C SSD163 de 128x64 avec connexion I2C
