# Fritzing sketch termostato Max (saved by Fritzing 0.9.3b)

parts:
  part = MAX6675 [package=so08]
  WeMos_D1_Mini1 = WeMos D1 Mini
  WiFiConfig = Pushbutton [package=THT]
  Relay = KY-019 5V Relay Module [package="Breakout board"]

nets:
  GND: part.VSS, WeMos_D1_Mini1.G, WiFiConfig.leg1, Relay.-
  VDD: part.VDD, WeMos_D1_Mini1.3V3
  N1: part.SCK, WeMos_D1_Mini1.D7
  N2: part.CS, WeMos_D1_Mini1.D6
  N3: part.MISO, WeMos_D1_Mini1.D5
  5V: WeMos_D1_Mini1.5V, Relay.+
  N4: WeMos_D1_Mini1.D1, Relay.S
  N5: WeMos_D1_Mini1.D3, WiFiConfig.leg0

custom parts:
  KY-019 5V Relay Module: KY-019 5V Relay module, used to control AC circuits.
